// Logisim project atm_final.circ as structural Verilog: 24 circuits, main circuit atm_final
module atm_final (
  input  [1:0] COD__SW0_1,
  input  [3:0] PIN__SW2_5,
  input  [15:0] in_3,
  input  [1:0] OP_SW6_7,
  input  SUMA__SW8,
  output [15:0] out_6,
  output [3:0] out_7,
  output [1:0] out_8,
  output [3:0] out_9,
  output [3:0] out_10,
  output [3:0] out_11,
  output [3:0] out_12,
  output [3:0] out_13,
  output [3:0] out_14,
  output [3:0] out_15,
  output [3:0] out_16,
  output [3:0] out_17,
  output [15:0] out_18,
  output [2:0] out_19
);

  wire afisor_1_a1, afisor_1_a2, afisor_1_a3, afisor_1_a4, afisor_1_b1, afisor_1_b2, afisor_1_b3,
       afisor_1_b4, afisor_1_c1, afisor_1_c2, afisor_1_c3, afisor_1_c4, afisor_1_d1, afisor_1_d2,
       afisor_1_d3, afisor_1_d4, afisor_1_e1, afisor_1_e2, afisor_1_e3, afisor_1_e4, afisor_1_f1,
       afisor_1_f2, afisor_1_f3, afisor_1_f4, afisor_1_g1, afisor_1_g2, afisor_1_g3, afisor_1_g4, and_1_out,
       and_2_out, B0_INT_CARD_out, CLOCK_out, comp4_biti_1_egal, comp4_biti_1_mare, comp4_biti_1_mic,
       comp_sold_1_ld, comp_sold_1_sold_ok, comparator_1000_1_ld, comparator_1000_1_ok, CONFIRM_out,
       controlled_buffer_1_out, d_ff_1_q, d_ff_2_q, d_ff_3_q, demultiplexer_1_out0, demultiplexer_1_out1,
       demultiplexer_1_out2, demultiplexer_1_out3, demultiplexer_4_out0, demultiplexer_4_out1,
       demultiplexer_5_out0, demultiplexer_5_out1, demultiplexer_5_out2, demultiplexer_5_out3,
       demultiplexer_7_out0, demultiplexer_7_out1, demultiplexer_7_out2, demultiplexer_7_out3,
       divizor_frecventa_1_clock_2, ENTER_out, memorare_1_bit_1_card_introdus,
       memorare_1_bit_2_card_introdus, memorare_1_bit_3_card_introdus, memorare_1_bit_4_card_introdus,
       memorare_1_bit_5_card_introdus, memorare_1_bit_6_card_introdus, not_1_out, not_2_out, or_1_out,
       or_2_out, or_3_out, or_4_out, or_5_out, or_6_out, or_7_out, or_8_out, or_9_out;
  wire [3:0] demultiplexer_3_out0, demultiplexer_3_out1, demultiplexer_3_out2, demultiplexer_3_out3,
       demultiplexer_6_out0, demultiplexer_6_out1, demultiplexer_6_out2, demultiplexer_6_out3,
       mem_rom_1_pin_rom, numarator_suma_1_out_5;
  wire [15:0] algoritm_1__5, algoritm_1__10, algoritm_1__20, algoritm_1__50, algoritm_1__100,
       algoritm_1__200, algoritm_1__500, multiplexer_1_out, scazator_1_out_4, sumator_bcd_16_biti_1_out;

  Button CONFIRM (.out(CONFIRM_out));
  LED LD0_CARD (.in(memorare_1_bit_1_card_introdus));
  Button B0_INT_CARD (.out(B0_INT_CARD_out));
  Clock CLOCK (.out(CLOCK_out));
  Button ENTER (.out(ENTER_out));
  LED LD1_PIN_GRESIT (.in(or_3_out));
  assign controlled_buffer_1_out = ENTER_out ? ENTER_out : 1'bz;  // Controlled_Buffer controlled_buffer_1
  LED LD2_INTEROGARE (.in(memorare_1_bit_4_card_introdus));
  LED LD3_DEPUNERE (.in(memorare_1_bit_3_card_introdus));
  MEMORARE_1_BIT memorare_1_bit_1 (
    .BUTON(B0_INT_CARD_out), .CLOCK(CLOCK_out), .RESET(memorare_1_bit_2_card_introdus),
    .CARD_INTRODUS(memorare_1_bit_1_card_introdus));
  LED LD6_SOLD_INSUFICIENT (.in(comp_sold_1_ld));
  LED LD5_1000 (.in(comparator_1000_1_ld));
  LED LD4_RETRAGERE (.in(memorare_1_bit_5_card_introdus));
  MEMORARE_1_BIT memorare_1_bit_2 (
    .BUTON(demultiplexer_1_out1), .CLOCK(ENTER_out), .RESET(1'b0),
    .CARD_INTRODUS(memorare_1_bit_2_card_introdus));
  _7_Segment_Display u_7_segment_display_1 (
    .g(afisor_1_g1), .f(afisor_1_f1), .a(afisor_1_a1), .b(afisor_1_b1), .e(afisor_1_e1), .d(afisor_1_d1),
    .c(afisor_1_c1), .dp(1'b0));
  MEM_ROM mem_rom_1 (.A_ROM(COD__SW0_1), .CS_ROM(memorare_1_bit_1_card_introdus), .PIN_ROM(mem_rom_1_pin_rom));
  Demultiplexer #(.select(2)) demultiplexer_1 (
    .out0(demultiplexer_1_out0), .out1(demultiplexer_1_out1), .out2(demultiplexer_1_out2),
    .out3(demultiplexer_1_out3), .in(comp4_biti_1_egal), .sel(OP_SW6_7), .en(comp4_biti_1_egal));
  MEMORARE_1_BIT memorare_1_bit_3 (
    .BUTON(demultiplexer_1_out2), .CLOCK(ENTER_out), .RESET(or_2_out),
    .CARD_INTRODUS(memorare_1_bit_3_card_introdus));
  _7_Segment_Display u_7_segment_display_2 (
    .g(afisor_1_g2), .f(afisor_1_f2), .a(afisor_1_a2), .b(afisor_1_b2), .e(afisor_1_e2), .d(afisor_1_d2),
    .c(afisor_1_c2), .dp(1'b0));
  MEMORARE_1_BIT memorare_1_bit_4 (
    .BUTON(demultiplexer_1_out0), .CLOCK(ENTER_out), .RESET(or_1_out),
    .CARD_INTRODUS(memorare_1_bit_4_card_introdus));
  or or_1 (or_1_out, demultiplexer_1_out2, demultiplexer_1_out3);
  or or_2 (or_2_out, demultiplexer_1_out0, demultiplexer_1_out3);
  comp4_biti comp4_biti_1 (
    .A(mem_rom_1_pin_rom), .MARE(comp4_biti_1_mare), .EGAL(comp4_biti_1_egal), .MIC(comp4_biti_1_mic),
    .CLK(CLOCK_out), .ENTER(controlled_buffer_1_out), .B(PIN__SW2_5));
  _7_Segment_Display u_7_segment_display_3 (
    .g(afisor_1_g3), .f(afisor_1_f3), .a(afisor_1_a3), .b(afisor_1_b3), .e(afisor_1_e3), .d(afisor_1_d3),
    .c(afisor_1_c3), .dp(1'b0));
  or or_3 (or_3_out, comp4_biti_1_mare, comp4_biti_1_mic);
  MEMORARE_1_BIT memorare_1_bit_5 (
    .BUTON(demultiplexer_1_out3), .CLOCK(ENTER_out), .RESET(or_4_out),
    .CARD_INTRODUS(memorare_1_bit_5_card_introdus));
  Multiplexer #(.width(16)) multiplexer_1 (
    .in0(sumator_bcd_16_biti_1_out), .in1(scazator_1_out_4), .out(multiplexer_1_out), .sel(OP_SW6_7[0]),
    .en(or_7_out));
  or or_4 (or_4_out, demultiplexer_1_out2, demultiplexer_1_out0);
  or or_5 (or_5_out, memorare_1_bit_4_card_introdus, memorare_1_bit_3_card_introdus, memorare_1_bit_5_card_introdus);
  _7_Segment_Display u_7_segment_display_4 (
    .g(afisor_1_g4), .f(afisor_1_f4), .a(afisor_1_a4), .b(afisor_1_b4), .e(afisor_1_e4), .d(afisor_1_d4),
    .c(afisor_1_c4), .dp(1'b0));
  or or_6 (or_6_out, memorare_1_bit_3_card_introdus, memorare_1_bit_5_card_introdus);
  MEMORIE_SOLD memorie_sold_1 (
    .COD(COD__SW0_1), .I_RAM(multiplexer_1_out), .INTRARE_DEMUX_INTEROGARE(or_5_out), .Sold(out_6),
    .clkc(CLOCK_out), .enter(CONFIRM_out));
  not not_1 (not_1_out, memorare_1_bit_3_card_introdus);
  not not_2 (not_2_out, memorare_1_bit_5_card_introdus);
  or or_7 (or_7_out, comparator_1000_1_ok, d_ff_1_q);
  MEMORARE_1_BIT memorare_1_bit_6 (
    .BUTON(or_6_out), .CLOCK(CLOCK_out), .RESET(or_8_out), .CARD_INTRODUS(memorare_1_bit_6_card_introdus));
  or or_8 (or_8_out, out_8[0], out_8[1]);
  NUMARATOR_SUMA numarator_suma_1 (
    .MODE(memorare_1_bit_6_card_introdus), .CLOCK(CLOCK_out), .SW(SUMA__SW8), .out_5(numarator_suma_1_out_5),
    .ENTER(ENTER_out));
  NUMARATOR_2_BITI numarator_2_biti_1 (.CLK(ENTER_out), .ENTER(or_6_out), .OUT(out_8));
  Demultiplexer #(.width(4), .enable("false")) demultiplexer_2 (
    .out0(out_10), .out1(out_16), .in(numarator_suma_1_out_5), .sel(OP_SW6_7[0]));
  Demultiplexer #(.select(2), .width(4), .enable("false")) demultiplexer_3 (
    .out0(demultiplexer_3_out0), .out1(demultiplexer_3_out1), .out2(demultiplexer_3_out2),
    .out3(demultiplexer_3_out3), .in(out_10), .sel(out_8));
  Demultiplexer #(.enable("false")) demultiplexer_4 (
    .out0(demultiplexer_4_out0), .out1(demultiplexer_4_out1), .in(or_6_out), .sel(OP_SW6_7[0]));
  Demultiplexer #(.select(2), .enable("false")) demultiplexer_5 (
    .out0(demultiplexer_5_out0), .out1(demultiplexer_5_out1), .out2(demultiplexer_5_out2),
    .out3(demultiplexer_5_out3), .in(SUMA__SW8), .sel(out_8));
  Demultiplexer #(.select(2), .width(4), .enable("false")) demultiplexer_6 (
    .out0(demultiplexer_6_out0), .out1(demultiplexer_6_out1), .out2(demultiplexer_6_out2),
    .out3(demultiplexer_6_out3), .in(out_16), .sel(out_8));
  Demultiplexer #(.select(2), .enable("false")) demultiplexer_7 (
    .out0(demultiplexer_7_out0), .out1(demultiplexer_7_out1), .out2(demultiplexer_7_out2),
    .out3(demultiplexer_7_out3), .in(SUMA__SW8), .sel(out_8));
  and and_1 (and_1_out, out_8[0], out_8[1]);
  D_Flip_Flop d_ff_1 (
    .clk(ENTER_out), .D(and_1_out), .Q(d_ff_1_q), .preset(1'b0), .en(demultiplexer_4_out0), .reset(1'b0));  // open: Qn
  MEMORARE_SUMA memorare_suma_1 (
    .SW(demultiplexer_5_out0), .R(not_1_out), .OUT(out_7), .CLOCK(CLOCK_out), .NR(demultiplexer_3_out0));
  MEMORARE_SUMA memorare_suma_2 (
    .SW(demultiplexer_5_out1), .R(not_1_out), .OUT(out_9), .CLOCK(CLOCK_out), .NR(demultiplexer_3_out1));
  MEMORARE_SUMA memorare_suma_3 (
    .SW(demultiplexer_5_out2), .R(not_1_out), .OUT(out_11), .CLOCK(CLOCK_out), .NR(demultiplexer_3_out2));
  MEMORARE_SUMA memorare_suma_4 (
    .SW(demultiplexer_5_out3), .R(not_1_out), .OUT(out_12), .CLOCK(CLOCK_out), .NR(demultiplexer_3_out3));
  MEMORARE_SUMA memorare_suma_5 (
    .SW(demultiplexer_7_out0), .R(not_2_out), .OUT(out_13), .CLOCK(CLOCK_out), .NR(demultiplexer_6_out0));
  MEMORARE_SUMA memorare_suma_6 (
    .SW(demultiplexer_7_out1), .R(not_2_out), .OUT(out_14), .CLOCK(CLOCK_out), .NR(demultiplexer_6_out1));
  MEMORARE_SUMA memorare_suma_7 (
    .SW(demultiplexer_7_out2), .R(not_2_out), .OUT(out_15), .CLOCK(CLOCK_out), .NR(demultiplexer_6_out2));
  MEMORARE_SUMA memorare_suma_8 (
    .SW(demultiplexer_7_out3), .R(not_2_out), .OUT(out_17), .CLOCK(CLOCK_out), .NR(demultiplexer_6_out3));
  and and_2 (and_2_out, out_8[0], out_8[1]);
  D_Flip_Flop d_ff_2 (
    .clk(ENTER_out), .D(and_2_out), .Q(d_ff_2_q), .preset(1'b0), .en(demultiplexer_4_out1), .reset(1'b0));  // open: Qn
  SUMATOR_BCD_16_BITI sumator_bcd_16_biti_1 (
    .A(out_6), .B({out_12, out_11, out_9, out_7}), .C(1'b0), .OUT(sumator_bcd_16_biti_1_out), .en(d_ff_1_q));
  COMPARATOR_1000 comparator_1000_1 (
    .enable(d_ff_2_q), .A(16'h1000), .clock(CLOCK_out), .B({out_17, out_15, out_14, out_13}),
    .LD(comparator_1000_1_ld), .OK(comparator_1000_1_ok));
  or or_9 (or_9_out, demultiplexer_1_out2, demultiplexer_1_out0);
  D_Flip_Flop d_ff_3 (
    .clk(CLOCK_out), .D(OP_SW6_7[0]), .Q(d_ff_3_q), .preset(1'b0), .en(CONFIRM_out), .reset(or_9_out));  // open: Qn
  COMP_SOLD comp_sold_1 (
    .ENABLE(comparator_1000_1_ok), .A(out_6), .B({out_17, out_15, out_14, out_13}),
    .SOLD_OK(comp_sold_1_sold_ok), .LD(comp_sold_1_ld), .clock(CLOCK_out));
  SCAZATOR scazator_1 (
    .A(out_6), .B({out_17, out_15, out_14, out_13}), .out_4(scazator_1_out_4), .EN(comp_sold_1_sold_ok));
  algoritm algoritm_1 (
    .EN(comp_sold_1_sold_ok), .SUMA({out_17, out_15, out_14, out_13}), ._500(algoritm_1__500),
    ._200(algoritm_1__200), ._100(algoritm_1__100), ._50(algoritm_1__50), ._20(algoritm_1__20),
    ._10(algoritm_1__10), ._5(algoritm_1__5), .clk(CLOCK_out), .R(or_9_out));  // open: NUM, out_5
  AFISOR afisor_1 (
    .SEL(OP_SW6_7), .A(out_6), .B(in_3), .C({out_12, out_11, out_9, out_7}),
    .E({out_17, out_15, out_14, out_13}), .F(algoritm_1__500), .G(algoritm_1__200), .H(algoritm_1__100),
    .I(algoritm_1__50), .J(algoritm_1__20), .K(algoritm_1__10), .num(out_19), .en(d_ff_3_q),
    .L(algoritm_1__5), .A1(afisor_1_a1), .A2(afisor_1_a2), .A3(afisor_1_a3), .A4(afisor_1_a4),
    .B3(afisor_1_b3), .B1(afisor_1_b1), .B2(afisor_1_b2), .B4(afisor_1_b4), .C2(afisor_1_c2),
    .C1(afisor_1_c1), .C3(afisor_1_c3), .C4(afisor_1_c4), .D1(afisor_1_d1), .D2(afisor_1_d2),
    .D3(afisor_1_d3), .D4(afisor_1_d4), .E1(afisor_1_e1), .E2(afisor_1_e2), .E3(afisor_1_e3),
    .E4(afisor_1_e4), .F1(afisor_1_f1), .F2(afisor_1_f2), .F3(afisor_1_f3), .F4(afisor_1_f4),
    .G1(afisor_1_g1), .G2(afisor_1_g2), .G3(afisor_1_g3), .G4(afisor_1_g4));
  num_3_biti num_3_biti_1 (.EN(d_ff_3_q), .clk(divizor_frecventa_1_clock_2), .r(1'b0), .out_4(out_19));
  DIVIZOR_FRECVENTA divizor_frecventa_1 (.CLOCK(CLOCK_out), .CLOCK_2(divizor_frecventa_1_clock_2));

  assign out_18 = {out_17, out_15, out_14, out_13};

  // Notes on the sheet:
  //   SUMA__SW8: pull=up
  //   00 - Interogare sold
  //   01 - Retragere card
  //   10 - Depunere numerar
  //   11 - Retragere numerar
endmodule

module COMPARATOR_4_BITI (
  input  E,
  input  A3,
  input  A2,
  input  A1,
  input  A0,
  input  B3,
  input  B2,
  input  B1,
  input  B0,
  output MAI_MARE,
  output EGAL,
  output MAI_MIC
);

  wire and_1_out, and_2_out, and_3_out, and_4_out, and_5_out, and_6_out, and_7_out, and_8_out, and_9_out,
       and_10_out, and_11_out, and_12_out, and_13_out, and_14_out, and_15_out, and_16_out, and_17_out,
       and_18_out, and_19_out, and_20_out, and_21_out, and_22_out, and_23_out, and_24_out, and_25_out,
       and_26_out, and_27_out, and_28_out, and_29_out, and_30_out, and_31_out, and_32_out, and_33_out,
       and_34_out, and_35_out, and_36_out, and_37_out, and_38_out, and_39_out, and_40_out, and_41_out,
       and_42_out, and_43_out, and_44_out, and_45_out, and_46_out, and_47_out, and_48_out, and_49_out,
       and_50_out, and_51_out, and_52_out, and_53_out, and_54_out, and_55_out, and_56_out, and_57_out,
       and_58_out, and_59_out, and_60_out, and_61_out, and_62_out, and_63_out, and_64_out, and_65_out,
       and_66_out, and_67_out, and_68_out, and_69_out, and_70_out, and_71_out, and_72_out, and_73_out,
       and_74_out, and_75_out, and_76_out, and_77_out, and_78_out, and_79_out, and_80_out, and_81_out,
       and_82_out, and_83_out, and_84_out, and_85_out, and_86_out, and_87_out, and_88_out, and_89_out,
       and_90_out, and_91_out, and_92_out, and_93_out, and_94_out, and_95_out, and_96_out, and_97_out,
       and_98_out, and_99_out, and_100_out, and_101_out, and_102_out, and_103_out, and_104_out, and_105_out,
       and_106_out, and_107_out, and_108_out, and_109_out, and_110_out, and_111_out, and_112_out,
       and_113_out, and_114_out, and_115_out, and_116_out, and_117_out, and_118_out, and_119_out,
       and_120_out, and_121_out, and_122_out, and_123_out, and_124_out, and_125_out, and_126_out,
       and_127_out, and_128_out, and_129_out, and_130_out, and_131_out, and_132_out, and_133_out,
       and_134_out, and_135_out, and_136_out, and_137_out, and_138_out, and_139_out, and_140_out,
       and_141_out, and_142_out, and_143_out, and_144_out, and_145_out, and_146_out, and_147_out,
       and_148_out, and_149_out, and_150_out, and_151_out, and_152_out, and_153_out, and_154_out,
       and_155_out, and_156_out, and_157_out, and_158_out, and_159_out, and_160_out, and_161_out,
       and_162_out, and_163_out, and_164_out, and_165_out, and_166_out, and_167_out, and_168_out,
       and_169_out, and_170_out, and_171_out, and_172_out, and_173_out, and_174_out, and_175_out,
       and_176_out, and_177_out, and_178_out, and_179_out, and_180_out, and_181_out, and_182_out,
       and_183_out, and_184_out, and_185_out, and_186_out, and_187_out, and_188_out, and_189_out,
       and_190_out, and_191_out, and_192_out, and_193_out, and_194_out, and_195_out, and_196_out,
       and_197_out, and_198_out, and_199_out, and_200_out, and_201_out, and_202_out, and_203_out,
       and_204_out, and_205_out, and_206_out, and_207_out, and_208_out, and_209_out, and_210_out,
       and_211_out, and_212_out, and_213_out, and_214_out, and_215_out, and_216_out, and_217_out,
       and_218_out, and_219_out, and_220_out, and_221_out, and_222_out, and_223_out, and_224_out,
       and_225_out, and_226_out, and_227_out, and_228_out, and_229_out, and_230_out, and_231_out,
       and_232_out, and_233_out, and_234_out, and_235_out, and_236_out, and_237_out, and_238_out,
       and_239_out, and_240_out, and_241_out, and_242_out, and_243_out, and_244_out, and_245_out,
       and_246_out, and_247_out, and_248_out, and_249_out, and_250_out, and_251_out, and_252_out,
       and_253_out, and_254_out, and_255_out, and_256_out, not_1_out, not_2_out, not_3_out, not_4_out,
       not_5_out, not_6_out, not_7_out, not_8_out, not_9_out, not_10_out, not_11_out, not_12_out, not_13_out,
       not_14_out, not_15_out, not_16_out, not_17_out, not_18_out, not_19_out, not_20_out, not_21_out,
       not_22_out, not_23_out, not_24_out, not_25_out, not_26_out, not_27_out, not_28_out, not_29_out,
       not_30_out, not_31_out, not_32_out, not_33_out, not_34_out, not_35_out, not_36_out, not_37_out,
       not_38_out, not_39_out, not_40_out, not_41_out, not_42_out, not_43_out, not_44_out, not_45_out,
       not_46_out, not_47_out, not_48_out, not_49_out, not_50_out, not_51_out, not_52_out, not_53_out,
       not_54_out, not_55_out, not_56_out, not_57_out, not_58_out, not_59_out, not_60_out, not_61_out,
       not_62_out, not_63_out, not_64_out, not_65_out, not_66_out, not_67_out, not_68_out, not_69_out,
       not_70_out, not_71_out, not_72_out, not_73_out, not_74_out, not_75_out, not_76_out, not_77_out,
       not_78_out, not_79_out, not_80_out, not_81_out, not_82_out, not_83_out, not_84_out, not_85_out,
       not_86_out, not_87_out, not_88_out, not_89_out, not_90_out, not_91_out, not_92_out, not_93_out,
       not_94_out, not_95_out, not_96_out, not_97_out, not_98_out, not_99_out, not_100_out, not_101_out,
       not_102_out, not_103_out, not_104_out, not_105_out, not_106_out, not_107_out, not_108_out,
       not_109_out, not_110_out, not_111_out, not_112_out, not_113_out, not_114_out, not_115_out,
       not_116_out, not_117_out, not_118_out, not_119_out, not_120_out, not_121_out, not_122_out,
       not_123_out, not_124_out, not_125_out, not_126_out, not_127_out, not_128_out, or_1_out, or_2_out,
       or_3_out, or_4_out, or_5_out, or_6_out, or_7_out, or_8_out, or_9_out, or_10_out, or_11_out, or_12_out,
       or_13_out, or_14_out, or_15_out, or_16_out, or_17_out, or_18_out, or_19_out, or_20_out, or_21_out,
       or_22_out, or_23_out, or_24_out, or_25_out, or_26_out, or_27_out, or_28_out, or_29_out, or_30_out,
       or_31_out, or_32_out, or_33_out, or_34_out, or_35_out, or_36_out, or_37_out, or_38_out, or_40_out,
       or_41_out;

  not not_1 (not_1_out, B2);
  not not_2 (not_2_out, B1);
  not not_3 (not_3_out, B3);
  not not_4 (not_4_out, B2);
  not not_5 (not_5_out, B3);
  not not_6 (not_6_out, B1);
  not not_7 (not_7_out, B3);
  not not_8 (not_8_out, B2);
  not not_9 (not_9_out, B1);
  not not_10 (not_10_out, B2);
  not not_11 (not_11_out, B1);
  not not_12 (not_12_out, A3);
  not not_13 (not_13_out, A3);
  not not_14 (not_14_out, A3);
  not not_15 (not_15_out, A3);
  not not_16 (not_16_out, A3);
  not not_17 (not_17_out, A3);
  not not_18 (not_18_out, A3);
  not not_19 (not_19_out, A3);
  not not_20 (not_20_out, A3);
  not not_21 (not_21_out, A1);
  not not_22 (not_22_out, A0);
  not not_23 (not_23_out, A3);
  not not_24 (not_24_out, A3);
  not not_25 (not_25_out, A0);
  not not_26 (not_26_out, A3);
  not not_27 (not_27_out, A0);
  not not_28 (not_28_out, A3);
  not not_29 (not_29_out, A3);
  not not_30 (not_30_out, A2);
  not not_31 (not_31_out, A0);
  not not_32 (not_32_out, A2);
  not not_33 (not_33_out, A2);
  not not_34 (not_34_out, A1);
  not not_35 (not_35_out, A1);
  and and_1 (and_1_out, E, A0);
  not not_36 (not_36_out, B3);
  and and_2 (and_2_out, not_1_out, not_2_out);
  not not_37 (not_37_out, B0);
  and and_3 (and_3_out, E, A1);
  not not_38 (not_38_out, B3);
  not not_39 (not_39_out, B2);
  not not_40 (not_40_out, B1);
  and and_4 (and_4_out, E, A1);
  and and_5 (and_5_out, not_3_out, not_4_out);
  not not_41 (not_41_out, B0);
  not not_42 (not_42_out, B3);
  not not_43 (not_43_out, B2);
  and and_6 (and_6_out, E, A2);
  and and_7 (and_7_out, not_5_out, not_6_out);
  not not_44 (not_44_out, B0);
  and and_8 (and_8_out, E, A2);
  not not_45 (not_45_out, B3);
  not not_46 (not_46_out, B1);
  and and_9 (and_9_out, E, A2);
  and and_10 (and_10_out, A0, not_7_out);
  not not_47 (not_47_out, B0);
  and and_11 (and_11_out, E, A3);
  and and_12 (and_12_out, not_8_out, not_9_out);
  not not_48 (not_48_out, B0);
  and and_13 (and_13_out, E, A3);
  not not_49 (not_49_out, B2);
  not not_50 (not_50_out, B1);
  and and_14 (and_14_out, E, A3);
  and and_15 (and_15_out, A0, not_10_out);
  not not_51 (not_51_out, B0);
  not not_52 (not_52_out, B2);
  and and_16 (and_16_out, E, A3);
  and and_17 (and_17_out, A0, not_11_out);
  not not_53 (not_53_out, B0);
  and and_18 (and_18_out, E, A3);
  not not_54 (not_54_out, B1);
  and and_19 (and_19_out, E, not_12_out);
  not not_55 (not_55_out, A2);
  not not_56 (not_56_out, A1);
  not not_57 (not_57_out, A0);
  not not_58 (not_58_out, B3);
  not not_59 (not_59_out, B2);
  not not_60 (not_60_out, B1);
  not not_61 (not_61_out, B0);
  and and_20 (and_20_out, E, not_13_out);
  not not_62 (not_62_out, A2);
  not not_63 (not_63_out, A1);
  not not_64 (not_64_out, B3);
  not not_65 (not_65_out, B2);
  not not_66 (not_66_out, B1);
  and and_21 (and_21_out, E, not_14_out);
  not not_67 (not_67_out, A2);
  not not_68 (not_68_out, A0);
  not not_69 (not_69_out, B3);
  not not_70 (not_70_out, B2);
  not not_71 (not_71_out, B0);
  and and_22 (and_22_out, E, not_15_out);
  not not_72 (not_72_out, A2);
  not not_73 (not_73_out, B3);
  not not_74 (not_74_out, B2);
  and and_23 (and_23_out, E, not_16_out);
  not not_75 (not_75_out, A1);
  not not_76 (not_76_out, A0);
  not not_77 (not_77_out, B3);
  not not_78 (not_78_out, B1);
  not not_79 (not_79_out, B0);
  and and_24 (and_24_out, E, not_17_out);
  not not_80 (not_80_out, A1);
  not not_81 (not_81_out, B3);
  not not_82 (not_82_out, B1);
  and and_25 (and_25_out, E, not_18_out);
  not not_83 (not_83_out, A0);
  not not_84 (not_84_out, B3);
  not not_85 (not_85_out, B0);
  and and_26 (and_26_out, E, not_19_out);
  not not_86 (not_86_out, B3);
  and and_27 (and_27_out, E, A3);
  not not_87 (not_87_out, A2);
  not not_88 (not_88_out, A1);
  not not_89 (not_89_out, A0);
  not not_90 (not_90_out, B2);
  not not_91 (not_91_out, B1);
  not not_92 (not_92_out, B0);
  and and_28 (and_28_out, E, A3);
  not not_93 (not_93_out, A2);
  not not_94 (not_94_out, A1);
  not not_95 (not_95_out, B2);
  not not_96 (not_96_out, B1);
  and and_29 (and_29_out, E, A3);
  not not_97 (not_97_out, A2);
  not not_98 (not_98_out, A0);
  not not_99 (not_99_out, B2);
  not not_100 (not_100_out, B0);
  and and_30 (and_30_out, E, A3);
  not not_101 (not_101_out, A2);
  not not_102 (not_102_out, B2);
  and and_31 (and_31_out, E, A3);
  not not_103 (not_103_out, A1);
  not not_104 (not_104_out, A0);
  not not_105 (not_105_out, B1);
  not not_106 (not_106_out, B0);
  and and_32 (and_32_out, E, A3);
  not not_107 (not_107_out, A1);
  not not_108 (not_108_out, B1);
  and and_33 (and_33_out, E, A3);
  not not_109 (not_109_out, A0);
  not not_110 (not_110_out, B0);
  and and_34 (and_34_out, E, A3);
  and and_35 (and_35_out, E, not_20_out);
  not not_111 (not_111_out, A2);
  and and_36 (and_36_out, not_21_out, not_22_out);
  and and_37 (and_37_out, E, not_23_out);
  not not_112 (not_112_out, A2);
  not not_113 (not_113_out, A1);
  and and_38 (and_38_out, E, not_24_out);
  not not_114 (not_114_out, A2);
  and and_39 (and_39_out, not_25_out, B1);
  not not_115 (not_115_out, A3);
  not not_116 (not_116_out, A2);
  and and_40 (and_40_out, E, not_26_out);
  not not_117 (not_117_out, A1);
  and and_41 (and_41_out, not_27_out, B2);
  and and_42 (and_42_out, E, not_28_out);
  not not_118 (not_118_out, A1);
  and and_43 (and_43_out, E, not_29_out);
  not not_119 (not_119_out, A0);
  and and_44 (and_44_out, B2, B1);
  not not_120 (not_120_out, A3);
  and and_45 (and_45_out, E, not_30_out);
  not not_121 (not_121_out, A1);
  and and_46 (and_46_out, not_31_out, B3);
  and and_47 (and_47_out, E, not_32_out);
  not not_122 (not_122_out, A1);
  and and_48 (and_48_out, E, not_33_out);
  not not_123 (not_123_out, A0);
  and and_49 (and_49_out, B3, B1);
  not not_124 (not_124_out, A2);
  and and_50 (and_50_out, E, not_34_out);
  not not_125 (not_125_out, A0);
  and and_51 (and_51_out, B3, B2);
  and and_52 (and_52_out, E, not_35_out);
  not not_126 (not_126_out, A0);
  and and_53 (and_53_out, and_1_out, not_36_out);
  and and_54 (and_54_out, and_53_out, and_55_out);
  and and_55 (and_55_out, and_2_out, not_37_out);
  and and_56 (and_56_out, and_3_out, not_38_out);
  and and_57 (and_57_out, and_56_out, and_58_out);
  and and_58 (and_58_out, not_39_out, not_40_out);
  and and_59 (and_59_out, and_4_out, A0);
  and and_60 (and_60_out, and_59_out, and_61_out);
  and and_61 (and_61_out, and_5_out, not_41_out);
  and and_62 (and_62_out, E, A2);
  and and_63 (and_63_out, and_62_out, and_64_out);
  and and_64 (and_64_out, not_42_out, not_43_out);
  and and_65 (and_65_out, and_6_out, A0);
  and and_66 (and_66_out, and_65_out, and_67_out);
  and and_67 (and_67_out, and_7_out, not_44_out);
  and and_68 (and_68_out, and_8_out, A1);
  and and_69 (and_69_out, and_68_out, and_70_out);
  and and_70 (and_70_out, not_45_out, not_46_out);
  and and_71 (and_71_out, and_9_out, A1);
  and and_72 (and_72_out, and_71_out, and_73_out);
  and and_73 (and_73_out, and_10_out, not_47_out);
  and and_74 (and_74_out, E, A3);
  and and_75 (and_75_out, and_74_out, not_127_out);
  not not_127 (not_127_out, B3);
  and and_76 (and_76_out, and_11_out, A0);
  and and_77 (and_77_out, and_76_out, and_78_out);
  and and_78 (and_78_out, and_12_out, not_48_out);
  and and_79 (and_79_out, and_13_out, A1);
  and and_80 (and_80_out, and_79_out, and_81_out);
  and and_81 (and_81_out, not_49_out, not_50_out);
  and and_82 (and_82_out, and_14_out, A1);
  and and_83 (and_83_out, and_82_out, and_84_out);
  and and_84 (and_84_out, and_15_out, not_51_out);
  and and_85 (and_85_out, E, A3);
  and and_86 (and_86_out, and_85_out, and_87_out);
  and and_87 (and_87_out, A2, not_52_out);
  and and_88 (and_88_out, and_16_out, A2);
  and and_89 (and_89_out, and_88_out, and_90_out);
  and and_90 (and_90_out, and_17_out, not_53_out);
  and and_91 (and_91_out, and_18_out, A2);
  and and_92 (and_92_out, and_91_out, and_93_out);
  and and_93 (and_93_out, A1, not_54_out);
  and and_94 (and_94_out, E, A3);
  and and_95 (and_95_out, and_94_out, A2);
  and and_96 (and_96_out, A1, A0);
  and and_97 (and_97_out, and_96_out, not_128_out);
  not not_128 (not_128_out, B0);
  and and_98 (and_98_out, and_19_out, not_55_out);
  and and_99 (and_99_out, and_98_out, and_100_out);
  and and_100 (and_100_out, not_56_out, not_57_out);
  and and_101 (and_101_out, not_58_out, not_59_out);
  and and_102 (and_102_out, and_101_out, and_103_out);
  and and_103 (and_103_out, not_60_out, not_61_out);
  and and_104 (and_104_out, and_20_out, not_62_out);
  and and_105 (and_105_out, and_104_out, and_106_out);
  and and_106 (and_106_out, not_63_out, A0);
  and and_107 (and_107_out, not_64_out, not_65_out);
  and and_108 (and_108_out, and_107_out, and_109_out);
  and and_109 (and_109_out, not_66_out, B0);
  and and_110 (and_110_out, and_21_out, not_67_out);
  and and_111 (and_111_out, and_110_out, and_112_out);
  and and_112 (and_112_out, A1, not_68_out);
  and and_113 (and_113_out, not_69_out, not_70_out);
  and and_114 (and_114_out, and_113_out, and_115_out);
  and and_115 (and_115_out, B1, not_71_out);
  and and_116 (and_116_out, and_22_out, not_72_out);
  and and_117 (and_117_out, and_116_out, and_118_out);
  and and_118 (and_118_out, A1, A0);
  and and_119 (and_119_out, not_73_out, not_74_out);
  and and_120 (and_120_out, and_119_out, and_121_out);
  and and_121 (and_121_out, B1, B0);
  and and_122 (and_122_out, and_23_out, A2);
  and and_123 (and_123_out, and_122_out, and_124_out);
  and and_124 (and_124_out, not_75_out, not_76_out);
  and and_125 (and_125_out, not_77_out, B2);
  and and_126 (and_126_out, and_125_out, and_127_out);
  and and_127 (and_127_out, not_78_out, not_79_out);
  and and_128 (and_128_out, and_24_out, A2);
  and and_129 (and_129_out, and_128_out, and_130_out);
  and and_130 (and_130_out, not_80_out, A0);
  and and_131 (and_131_out, not_81_out, B2);
  and and_132 (and_132_out, and_131_out, and_133_out);
  and and_133 (and_133_out, not_82_out, B0);
  and and_134 (and_134_out, and_25_out, A2);
  and and_135 (and_135_out, and_134_out, and_136_out);
  and and_136 (and_136_out, A1, not_83_out);
  and and_137 (and_137_out, not_84_out, B2);
  and and_138 (and_138_out, and_137_out, and_139_out);
  and and_139 (and_139_out, B1, not_85_out);
  and and_140 (and_140_out, and_26_out, A2);
  and and_141 (and_141_out, and_140_out, and_142_out);
  and and_142 (and_142_out, A1, A0);
  and and_143 (and_143_out, not_86_out, B2);
  and and_144 (and_144_out, and_143_out, and_145_out);
  and and_145 (and_145_out, B1, B0);
  and and_146 (and_146_out, and_27_out, not_87_out);
  and and_147 (and_147_out, and_146_out, and_148_out);
  and and_148 (and_148_out, not_88_out, not_89_out);
  and and_149 (and_149_out, B3, not_90_out);
  and and_150 (and_150_out, and_149_out, and_151_out);
  and and_151 (and_151_out, not_91_out, not_92_out);
  and and_152 (and_152_out, and_28_out, not_93_out);
  and and_153 (and_153_out, and_152_out, and_154_out);
  and and_154 (and_154_out, not_94_out, A0);
  and and_155 (and_155_out, B3, not_95_out);
  and and_156 (and_156_out, and_155_out, and_157_out);
  and and_157 (and_157_out, not_96_out, B0);
  and and_158 (and_158_out, and_29_out, not_97_out);
  and and_159 (and_159_out, and_158_out, and_160_out);
  and and_160 (and_160_out, A1, not_98_out);
  and and_161 (and_161_out, B3, not_99_out);
  and and_162 (and_162_out, and_161_out, and_163_out);
  and and_163 (and_163_out, B1, not_100_out);
  and and_164 (and_164_out, and_30_out, not_101_out);
  and and_165 (and_165_out, and_164_out, and_166_out);
  and and_166 (and_166_out, A1, A0);
  and and_167 (and_167_out, B3, not_102_out);
  and and_168 (and_168_out, and_167_out, and_169_out);
  and and_169 (and_169_out, B1, B0);
  and and_170 (and_170_out, and_31_out, A2);
  and and_171 (and_171_out, and_170_out, and_172_out);
  and and_172 (and_172_out, not_103_out, not_104_out);
  and and_173 (and_173_out, B3, B2);
  and and_174 (and_174_out, and_173_out, and_175_out);
  and and_175 (and_175_out, not_105_out, not_106_out);
  and and_176 (and_176_out, and_32_out, A2);
  and and_177 (and_177_out, and_176_out, and_178_out);
  and and_178 (and_178_out, not_107_out, A0);
  and and_179 (and_179_out, B3, B2);
  and and_180 (and_180_out, and_179_out, and_181_out);
  and and_181 (and_181_out, not_108_out, B0);
  and and_182 (and_182_out, and_33_out, A2);
  and and_183 (and_183_out, and_182_out, and_184_out);
  and and_184 (and_184_out, A1, not_109_out);
  and and_185 (and_185_out, B3, B2);
  and and_186 (and_186_out, and_185_out, and_187_out);
  and and_187 (and_187_out, B1, not_110_out);
  and and_188 (and_188_out, and_34_out, A2);
  and and_189 (and_189_out, and_188_out, and_190_out);
  and and_190 (and_190_out, A1, A0);
  and and_191 (and_191_out, B3, B2);
  and and_192 (and_192_out, and_191_out, and_193_out);
  and and_193 (and_193_out, B1, B0);
  and and_194 (and_194_out, and_35_out, not_111_out);
  and and_195 (and_195_out, and_194_out, and_196_out);
  and and_196 (and_196_out, and_36_out, B0);
  and and_197 (and_197_out, and_37_out, not_112_out);
  and and_198 (and_198_out, and_197_out, and_199_out);
  and and_199 (and_199_out, not_113_out, B1);
  and and_200 (and_200_out, and_38_out, not_114_out);
  and and_201 (and_201_out, and_200_out, and_202_out);
  and and_202 (and_202_out, and_39_out, B0);
  and and_203 (and_203_out, E, not_115_out);
  and and_204 (and_204_out, and_203_out, and_205_out);
  and and_205 (and_205_out, not_116_out, B2);
  and and_206 (and_206_out, and_40_out, not_117_out);
  and and_207 (and_207_out, and_206_out, and_208_out);
  and and_208 (and_208_out, and_41_out, B0);
  and and_209 (and_209_out, and_42_out, not_118_out);
  and and_210 (and_210_out, and_209_out, and_211_out);
  and and_211 (and_211_out, B2, B1);
  and and_212 (and_212_out, and_43_out, not_119_out);
  and and_213 (and_213_out, and_212_out, and_214_out);
  and and_214 (and_214_out, and_44_out, B0);
  and and_215 (and_215_out, E, not_120_out);
  and and_216 (and_216_out, and_215_out, B3);
  and and_217 (and_217_out, and_45_out, not_121_out);
  and and_218 (and_218_out, and_217_out, and_219_out);
  and and_219 (and_219_out, and_46_out, B0);
  and and_220 (and_220_out, and_47_out, not_122_out);
  and and_221 (and_221_out, and_220_out, and_222_out);
  and and_222 (and_222_out, B3, B1);
  and and_223 (and_223_out, and_48_out, not_123_out);
  and and_224 (and_224_out, and_223_out, and_225_out);
  and and_225 (and_225_out, and_49_out, B0);
  and and_226 (and_226_out, E, not_124_out);
  and and_227 (and_227_out, and_226_out, and_228_out);
  and and_228 (and_228_out, B3, B2);
  and and_229 (and_229_out, and_50_out, not_125_out);
  and and_230 (and_230_out, and_229_out, and_231_out);
  and and_231 (and_231_out, and_51_out, B0);
  and and_232 (and_232_out, and_52_out, B3);
  and and_233 (and_233_out, and_232_out, and_234_out);
  and and_234 (and_234_out, B2, B1);
  and and_235 (and_235_out, E, not_126_out);
  and and_236 (and_236_out, and_235_out, B3);
  and and_237 (and_237_out, B2, B1);
  and and_238 (and_238_out, and_237_out, B0);
  or or_1 (or_1_out, and_54_out, and_57_out);
  or or_2 (or_2_out, and_60_out, and_63_out);
  or or_3 (or_3_out, and_66_out, and_69_out);
  or or_4 (or_4_out, and_72_out, and_75_out);
  or or_5 (or_5_out, and_77_out, and_80_out);
  or or_6 (or_6_out, and_83_out, and_86_out);
  or or_7 (or_7_out, and_89_out, and_92_out);
  and and_239 (and_239_out, and_95_out, and_97_out);
  and and_240 (and_240_out, and_99_out, and_102_out);
  and and_241 (and_241_out, and_105_out, and_108_out);
  and and_242 (and_242_out, and_111_out, and_114_out);
  and and_243 (and_243_out, and_117_out, and_120_out);
  and and_244 (and_244_out, and_123_out, and_126_out);
  and and_245 (and_245_out, and_129_out, and_132_out);
  and and_246 (and_246_out, and_135_out, and_138_out);
  and and_247 (and_247_out, and_141_out, and_144_out);
  and and_248 (and_248_out, and_147_out, and_150_out);
  and and_249 (and_249_out, and_153_out, and_156_out);
  and and_250 (and_250_out, and_159_out, and_162_out);
  and and_251 (and_251_out, and_165_out, and_168_out);
  and and_252 (and_252_out, and_171_out, and_174_out);
  and and_253 (and_253_out, and_177_out, and_180_out);
  and and_254 (and_254_out, and_183_out, and_186_out);
  and and_255 (and_255_out, and_189_out, and_192_out);
  or or_8 (or_8_out, and_195_out, and_198_out);
  or or_9 (or_9_out, and_201_out, and_204_out);
  or or_10 (or_10_out, and_207_out, and_210_out);
  or or_11 (or_11_out, and_213_out, and_216_out);
  or or_12 (or_12_out, and_218_out, and_221_out);
  or or_13 (or_13_out, and_224_out, and_227_out);
  or or_14 (or_14_out, and_230_out, and_233_out);
  and and_256 (and_256_out, and_236_out, and_238_out);
  or or_15 (or_15_out, or_1_out, or_2_out);
  or or_16 (or_16_out, or_3_out, or_4_out);
  or or_17 (or_17_out, or_5_out, or_6_out);
  or or_18 (or_18_out, or_7_out, and_239_out);
  or or_19 (or_19_out, and_240_out, and_241_out);
  or or_20 (or_20_out, and_242_out, and_243_out);
  or or_21 (or_21_out, and_244_out, and_245_out);
  or or_22 (or_22_out, and_246_out, and_247_out);
  or or_23 (or_23_out, and_248_out, and_249_out);
  or or_24 (or_24_out, and_250_out, and_251_out);
  or or_25 (or_25_out, and_252_out, and_253_out);
  or or_26 (or_26_out, and_254_out, and_255_out);
  or or_27 (or_27_out, or_8_out, or_9_out);
  or or_28 (or_28_out, or_10_out, or_11_out);
  or or_29 (or_29_out, or_12_out, or_13_out);
  or or_30 (or_30_out, or_14_out, and_256_out);
  or or_31 (or_31_out, or_15_out, or_16_out);
  or or_32 (or_32_out, or_17_out, or_18_out);
  or or_33 (or_33_out, or_19_out, or_20_out);
  or or_34 (or_34_out, or_21_out, or_22_out);
  or or_35 (or_35_out, or_23_out, or_24_out);
  or or_36 (or_36_out, or_25_out, or_26_out);
  or or_37 (or_37_out, or_27_out, or_28_out);
  or or_38 (or_38_out, or_29_out, or_30_out);
  or or_39 (MAI_MARE, or_31_out, or_32_out);
  or or_40 (or_40_out, or_33_out, or_34_out);
  or or_41 (or_41_out, or_35_out, or_36_out);
  or or_42 (MAI_MIC, or_37_out, or_38_out);
  or or_43 (EGAL, or_40_out, or_41_out);
endmodule

// COMPARATOR PIN
module comp4_biti (
  input  CLK,
  input  [3:0] A,
  input  [3:0] B,
  input  ENTER,
  output MARE,
  output EGAL,
  output MIC
);

  wire d_ff_1_q;

  D_Flip_Flop d_ff_1 (.clk(CLK), .D(ENTER), .Q(d_ff_1_q), .preset(1'b0), .en(ENTER), .reset(1'b0));  // open: Qn
  COMPARATOR_4_BITI comparator_4_biti_1 (
    .E(d_ff_1_q), .A3(A[3]), .A2(A[2]), .A1(A[1]), .A0(A[0]), .B3(B[3]), .B2(B[2]), .B1(B[1]), .B0(B[0]),
    .MAI_MARE(MARE), .EGAL(EGAL), .MAI_MIC(MIC));
endmodule

module REGISTRU_MEMORARE_4BITI (
  input  [3:0] PIN,
  input  CLOCK,
  input  ENTER,
  input  R,
  output [3:0] PIN_2
);

  D_Flip_Flop d_ff_1 (.clk(CLOCK), .D(PIN[3]), .Q(PIN_2[3]), .en(ENTER), .reset(R));  // open: Qn, preset
  D_Flip_Flop d_ff_2 (.clk(CLOCK), .D(PIN[2]), .Q(PIN_2[2]), .en(ENTER), .reset(R));  // open: Qn, preset
  D_Flip_Flop d_ff_3 (.clk(CLOCK), .D(PIN[1]), .Q(PIN_2[1]), .en(ENTER), .reset(R));  // open: Qn, preset
  D_Flip_Flop d_ff_4 (.clk(CLOCK), .D(PIN[0]), .Q(PIN_2[0]), .en(ENTER), .reset(R));  // open: Qn, preset
endmodule

// NUMARATOR MODULO 4
module NUMARATOR_2_BITI (
  input  CLK,
  input  ENTER,
  output [1:0] OUT
);

  wire d_ff_2_qn, xor_1_out;

  xor xor_1 (xor_1_out, OUT[0], OUT[1]);
  D_Flip_Flop d_ff_1 (.clk(CLK), .D(xor_1_out), .Q(OUT[1]), .en(ENTER));  // open: Qn, preset, reset
  D_Flip_Flop d_ff_2 (.clk(CLK), .D(d_ff_2_qn), .Q(OUT[0]), .Qn(d_ff_2_qn), .en(ENTER));  // open: preset, reset
endmodule

module REGISTRU_MEMORARE_2_BITI (
  input  [1:0] SW_OPERATIE,
  input  CLOCK,
  input  ENABLE,
  output [1:0] OPERATIE
);

  D_Flip_Flop d_ff_1 (.clk(CLOCK), .D(SW_OPERATIE[1]), .Q(OPERATIE[1]), .en(ENABLE));  // open: Qn, preset, reset
  D_Flip_Flop d_ff_2 (.clk(CLOCK), .D(SW_OPERATIE[0]), .Q(OPERATIE[0]), .en(ENABLE));  // open: Qn, preset, reset
endmodule

// AFISARE DATE
module AFISOR (
  input  [1:0] SEL,
  input  [15:0] A,
  input  [15:0] B,
  input  [15:0] C,
  input  [15:0] E,
  input  [15:0] F,
  input  [15:0] G,
  input  [15:0] H,
  input  [15:0] I,
  input  [15:0] J,
  input  [15:0] K,
  input  [2:0] num,
  input  en,
  input  [15:0] L,
  output A1,
  output A2,
  output A3,
  output A4,
  output B3,
  output B1,
  output B2,
  output B4,
  output C2,
  output C1,
  output C3,
  output C4,
  output D1,
  output D2,
  output D3,
  output D4,
  output E1,
  output E2,
  output E3,
  output E4,
  output F1,
  output F2,
  output F3,
  output F4,
  output G1,
  output G2,
  output G3,
  output G4
);

  wire a1_t, a2_t, a3_t, a4_t, a5, a6, a7, a8, a9, a10, a11, a12, a13, a14, a15, a16, a17, a18, a19, a20,
       a21, a22, a23, a24, a25, a26, a27, a28, a29, a30, a31, a32, a33, a34, a35, a36, a37, a38, a39, a40,
       a41, a42, a43, a44, b1_t, b2_t, b3_t, b4_t, b5, b6, b7, b8, b9, b10, b11, b12, b13, b14, b15, b16,
       b17, b18, b19, b20, b21, b22, b23, b24, b25, b26, b27, b28, b29, b30, b31, b32, b33, b34, b35, b36,
       b37, b38, b39, b40, b41, b42, b43, b44, c1_t, c2_t, c3_t, c4_t, c5, c6, c7, c8, c9, c10, c11, c12,
       c13, c14, c15, c16, c17, c18, c19, c20, c21, c22, c23, c24, c25, c26, c27, c28, c29, c30, c31, c32,
       c33, c34, c35, c36, c37, c38, c39, c40, c41, c42, c43, c44, d1_t, d2_t, d3_t, d4_t, d5, d6, d7, d8,
       d9, d10, d11, d12, d13, d14, d15, d16, d17, d18, d19, d20, d21, d22, d23, d24, d25, d26, d27, d28,
       d29, d30, d31, d32, d33, d34, d35, d36, d37, d38, d39, d40, d41, d42, d43, d44, e1_t, e2_t, e3_t,
       e4_t, e5, e6, e7, e8, e9, e10, e11, e12, e13, e14, e15, e16, e17, e18, e19, e20, e21, e22, e23, e24,
       e25, e26, e27, e28, e29, e30, e31, e32, e33, e34, e35, e36, e37, e38, e39, e40, e41, e42, e43, e44,
       f1_t, f2_t, f3_t, f4_t, f5, f5_t, f6, f7, f8, f9, f10, f11, f12, f13, f14, f15, f15_t, f16, f17, f18,
       f19, f20, f21, f22, f23, f24, f25, f25_t, f26, f27, f28, f29, f30, f31, f32, f33, f34, f35, f36, f37,
       f38, f39, f40, f41, f42, f43, f44, g1_t, g2_t, g3_t, g4_t, g5, g6, g7, g8, g9, g10, g11, g12, g13,
       g14, g15, g16, g17, g18, g19, g20, g21, g22, g23, g24, g25, g26, g27, g28, g29, g30, g31, g32, g33,
       g34, g35, g36, g37, g38, g39, g40, g41, g42, g43, g44, multiplexer_1_out, multiplexer_2_out,
       multiplexer_3_out, multiplexer_4_out, multiplexer_5_out, multiplexer_6_out, multiplexer_7_out,
       multiplexer_8_out, multiplexer_9_out, multiplexer_10_out, multiplexer_11_out, multiplexer_12_out,
       multiplexer_13_out, multiplexer_14_out, multiplexer_22_out, multiplexer_23_out, multiplexer_24_out,
       multiplexer_25_out, multiplexer_26_out, multiplexer_27_out, multiplexer_28_out, multiplexer_29_out,
       multiplexer_30_out, multiplexer_31_out, multiplexer_32_out, multiplexer_33_out, multiplexer_34_out,
       multiplexer_35_out, multiplexer_43_out, multiplexer_44_out, multiplexer_45_out, multiplexer_46_out,
       multiplexer_47_out, multiplexer_48_out, multiplexer_49_out, multiplexer_50_out, multiplexer_51_out,
       multiplexer_52_out, multiplexer_53_out, multiplexer_54_out, multiplexer_55_out, multiplexer_56_out,
       multiplexer_64_out, multiplexer_65_out, multiplexer_66_out, multiplexer_67_out, multiplexer_68_out,
       multiplexer_69_out, multiplexer_70_out, multiplexer_71_out, multiplexer_72_out, multiplexer_73_out,
       multiplexer_74_out, multiplexer_75_out, multiplexer_76_out, multiplexer_77_out;

  Multiplexer #(.select(2), .enable("false")) multiplexer_1 (
    .in0(a1_t), .in1(a2_t), .in2(a3_t), .in3(a4_t), .out(multiplexer_1_out), .sel(SEL));
  Multiplexer #(.select(2), .enable("false")) multiplexer_2 (
    .in0(b1_t), .in1(b2_t), .in2(b3_t), .in3(b4_t), .out(multiplexer_2_out), .sel(SEL));
  Multiplexer #(.select(2), .enable("false")) multiplexer_3 (
    .in0(c1_t), .in1(c2_t), .in2(c3_t), .in3(c4_t), .out(multiplexer_3_out), .sel(SEL));
  Multiplexer #(.select(2), .enable("false")) multiplexer_4 (
    .in0(d1_t), .in1(d2_t), .in2(d3_t), .in3(d4_t), .out(multiplexer_4_out), .sel(SEL));
  Multiplexer #(.select(2), .enable("false")) multiplexer_5 (
    .in0(e1_t), .in1(e2_t), .in2(e3_t), .in3(e4_t), .out(multiplexer_5_out), .sel(SEL));
  Multiplexer #(.select(2), .enable("false")) multiplexer_6 (
    .in0(f1_t), .in1(f2_t), .in2(f3_t), .in3(f4_t), .out(multiplexer_6_out), .sel(SEL));
  Multiplexer #(.select(2), .enable("false")) multiplexer_7 (
    .in0(g1_t), .in1(g2_t), .in2(g3_t), .in3(g4_t), .out(multiplexer_7_out), .sel(SEL));
  Multiplexer #(.select(3)) multiplexer_8 (
    .in0(a5), .in1(a6), .in2(a7), .in3(a8), .in4(a9), .in5(a10), .in6(a41), .out(multiplexer_8_out),
    .sel(num), .en(en));  // open: in7
  Multiplexer #(.select(3)) multiplexer_9 (
    .in0(b5), .in1(b6), .in2(b7), .in3(b8), .in4(b9), .in5(b10), .in6(b41), .out(multiplexer_9_out),
    .sel(num), .en(en));  // open: in7
  Multiplexer #(.select(3)) multiplexer_10 (
    .in0(c5), .in1(c6), .in2(c7), .in3(c8), .in4(c9), .in5(c10), .in6(c41), .out(multiplexer_10_out),
    .sel(num), .en(en));  // open: in7
  Multiplexer #(.select(3)) multiplexer_11 (
    .in0(d5), .in1(d6), .in2(d7), .in3(d8), .in4(d9), .in5(d10), .in6(d41), .out(multiplexer_11_out),
    .sel(num), .en(en));  // open: in7
  Multiplexer #(.select(3)) multiplexer_12 (
    .in0(e5), .in1(e6), .in2(e7), .in3(e8), .in4(e9), .in5(e10), .in6(e41), .out(multiplexer_12_out),
    .sel(num), .en(en));  // open: in7
  Multiplexer #(.select(3)) multiplexer_13 (
    .in0(f5), .in1(f6), .in2(f7), .in3(f8), .in4(f9), .in5(f10), .in6(f41), .out(multiplexer_13_out),
    .sel(num), .en(en));  // open: in7
  Multiplexer #(.select(3)) multiplexer_14 (
    .in0(g5), .in1(g6), .in2(g7), .in3(g8), .in4(g9), .in5(g10), .in6(g41), .out(multiplexer_14_out),
    .sel(num), .en(en));  // open: in7
  Multiplexer #(.enable("false")) multiplexer_15 (.in0(multiplexer_1_out), .in1(multiplexer_8_out), .out(A1), .sel(en));
  Multiplexer #(.enable("false")) multiplexer_16 (.in0(multiplexer_2_out), .in1(multiplexer_9_out), .out(B1), .sel(en));
  Multiplexer #(.enable("false")) multiplexer_17 (
    .in0(multiplexer_3_out), .in1(multiplexer_10_out), .out(C1), .sel(en));
  Multiplexer #(.enable("false")) multiplexer_18 (
    .in0(multiplexer_4_out), .in1(multiplexer_11_out), .out(D1), .sel(en));
  Multiplexer #(.enable("false")) multiplexer_19 (
    .in0(multiplexer_5_out), .in1(multiplexer_12_out), .out(E1), .sel(en));
  Multiplexer #(.enable("false")) multiplexer_20 (
    .in0(multiplexer_6_out), .in1(multiplexer_13_out), .out(F1), .sel(en));
  Multiplexer #(.enable("false")) multiplexer_21 (
    .in0(multiplexer_7_out), .in1(multiplexer_14_out), .out(G1), .sel(en));
  DECODIFICATOR_7_SEG decodificator_7_seg_1 (
    .A(A[15]), .B(A[14]), .C(A[13]), .D(A[12]), .a_2(a1_t), .b_2(b1_t), .c_2(c1_t), .d_2(d1_t), .e(e1_t),
    .f(f1_t), .g(g1_t));
  DECODIFICATOR_7_SEG decodificator_7_seg_2 (
    .A(B[15]), .B(B[14]), .C(B[13]), .D(B[12]), .a_2(a2_t), .b_2(b2_t), .c_2(c2_t), .d_2(d2_t), .e(e2_t),
    .f(f2_t), .g(g2_t));
  DECODIFICATOR_7_SEG decodificator_7_seg_3 (
    .A(C[15]), .B(C[14]), .C(C[13]), .D(C[12]), .a_2(a3_t), .b_2(b3_t), .c_2(c3_t), .d_2(d3_t), .e(e3_t),
    .f(f3_t), .g(g3_t));
  DECODIFICATOR_7_SEG decodificator_7_seg_4 (
    .A(E[15]), .B(E[14]), .C(E[13]), .D(E[12]), .a_2(a4_t), .b_2(b4_t), .c_2(c4_t), .d_2(d4_t), .e(e4_t),
    .f(f4_t), .g(g4_t));
  DECODIFICATOR_7_SEG decodificator_7_seg_5 (
    .A(F[15]), .B(F[14]), .C(F[13]), .D(F[12]), .a_2(a5), .b_2(b5), .c_2(c5), .d_2(d5), .e(e5), .f(f5_t),
    .g(g5));
  DECODIFICATOR_7_SEG decodificator_7_seg_6 (
    .A(G[15]), .B(G[14]), .C(G[13]), .D(G[12]), .a_2(a6), .b_2(b6), .c_2(c6), .d_2(d6), .e(e6), .f(f6), .g(g6));
  DECODIFICATOR_7_SEG decodificator_7_seg_7 (
    .A(H[15]), .B(H[14]), .C(H[13]), .D(H[12]), .a_2(a7), .b_2(b7), .c_2(c7), .d_2(d7), .e(e7), .f(f7), .g(g7));
  DECODIFICATOR_7_SEG decodificator_7_seg_8 (
    .A(I[15]), .B(I[14]), .C(I[13]), .D(I[12]), .a_2(a8), .b_2(b8), .c_2(c8), .d_2(d8), .e(e8), .f(f8), .g(g8));
  DECODIFICATOR_7_SEG decodificator_7_seg_9 (
    .A(J[15]), .B(J[14]), .C(J[13]), .D(J[12]), .a_2(a9), .b_2(b9), .c_2(c9), .d_2(d9), .e(e9), .f(f9), .g(g9));
  DECODIFICATOR_7_SEG decodificator_7_seg_10 (
    .A(K[15]), .B(K[14]), .C(K[13]), .D(K[12]), .a_2(a10), .b_2(b10), .c_2(c10), .d_2(d10), .e(e10), .f(f10),
    .g(g10));
  Multiplexer #(.select(2), .enable("false")) multiplexer_22 (
    .in0(a11), .in1(a12), .in2(a13), .in3(a14), .out(multiplexer_22_out), .sel(SEL));
  Multiplexer #(.select(2), .enable("false")) multiplexer_23 (
    .in0(b11), .in1(b12), .in2(b13), .in3(b14), .out(multiplexer_23_out), .sel(SEL));
  Multiplexer #(.select(2), .enable("false")) multiplexer_24 (
    .in0(c11), .in1(c12), .in2(c13), .in3(c14), .out(multiplexer_24_out), .sel(SEL));
  Multiplexer #(.select(2), .enable("false")) multiplexer_25 (
    .in0(d11), .in1(d12), .in2(d13), .in3(d14), .out(multiplexer_25_out), .sel(SEL));
  Multiplexer #(.select(2), .enable("false")) multiplexer_26 (
    .in0(e11), .in1(e12), .in2(e13), .in3(e14), .out(multiplexer_26_out), .sel(SEL));
  Multiplexer #(.select(2), .enable("false")) multiplexer_27 (
    .in0(f11), .in1(f12), .in2(f13), .in3(f14), .out(multiplexer_27_out), .sel(SEL));
  Multiplexer #(.select(2), .enable("false")) multiplexer_28 (
    .in0(g11), .in1(g12), .in2(g13), .in3(g14), .out(multiplexer_28_out), .sel(SEL));
  Multiplexer #(.select(3)) multiplexer_29 (
    .in0(a15), .in1(a16), .in2(a17), .in3(a18), .in4(a19), .in5(a20), .in6(a42), .out(multiplexer_29_out),
    .sel(num), .en(en));  // open: in7
  DECODIFICATOR_7_SEG decodificator_7_seg_11 (
    .A(L[15]), .B(L[14]), .C(L[13]), .D(L[12]), .a_2(a41), .b_2(b41), .c_2(c41), .d_2(d41), .e(e41), .f(f41),
    .g(g41));
  Multiplexer #(.select(3)) multiplexer_30 (
    .in0(b15), .in1(b16), .in2(b17), .in3(b18), .in4(b19), .in5(b20), .in6(b42), .out(multiplexer_30_out),
    .sel(num), .en(en));  // open: in7
  Multiplexer #(.select(3)) multiplexer_31 (
    .in0(c15), .in1(c16), .in2(c17), .in3(c18), .in4(c19), .in5(c20), .in6(c42), .out(multiplexer_31_out),
    .sel(num), .en(en));  // open: in7
  Multiplexer #(.select(3)) multiplexer_32 (
    .in0(d15), .in2(d16), .in3(d17), .in4(d18), .in5(d19), .in6(d20), .in7(d42), .out(multiplexer_32_out),
    .sel(num), .en(en));  // open: in1
  Multiplexer #(.select(3)) multiplexer_33 (
    .in0(e15), .in1(e16), .in2(e17), .in3(e18), .in4(e19), .in5(e20), .in6(e42), .out(multiplexer_33_out),
    .sel(num), .en(en));  // open: in7
  Multiplexer #(.select(3)) multiplexer_34 (
    .in0(f15), .in1(f16), .in2(f17), .in3(f18), .in4(f19), .in5(f20), .in6(f42), .out(multiplexer_34_out),
    .sel(num), .en(en));  // open: in7
  Multiplexer #(.select(3)) multiplexer_35 (
    .in0(g15), .in1(g16), .in2(g17), .in3(g18), .in4(g19), .in5(g20), .in6(g42), .out(multiplexer_35_out),
    .sel(num), .en(en));  // open: in7
  Multiplexer #(.enable("false")) multiplexer_36 (
    .in0(multiplexer_22_out), .in1(multiplexer_29_out), .out(A2), .sel(en));
  Multiplexer #(.enable("false")) multiplexer_37 (
    .in0(multiplexer_23_out), .in1(multiplexer_30_out), .out(B2), .sel(en));
  Multiplexer #(.enable("false")) multiplexer_38 (
    .in0(multiplexer_24_out), .in1(multiplexer_31_out), .out(C2), .sel(en));
  Multiplexer #(.enable("false")) multiplexer_39 (
    .in0(multiplexer_25_out), .in1(multiplexer_32_out), .out(D2), .sel(en));
  Multiplexer #(.enable("false")) multiplexer_40 (
    .in0(multiplexer_26_out), .in1(multiplexer_33_out), .out(E2), .sel(en));
  Multiplexer #(.enable("false")) multiplexer_41 (
    .in0(multiplexer_27_out), .in1(multiplexer_34_out), .out(F2), .sel(en));
  Multiplexer #(.enable("false")) multiplexer_42 (
    .in0(multiplexer_28_out), .in1(multiplexer_35_out), .out(G2), .sel(en));
  DECODIFICATOR_7_SEG decodificator_7_seg_12 (
    .A(F[11]), .B(F[10]), .C(F[9]), .D(F[8]), .a_2(a15), .b_2(b15), .c_2(c15), .d_2(d15), .e(e15), .f(f15_t),
    .g(g15));
  DECODIFICATOR_7_SEG decodificator_7_seg_13 (
    .A(G[11]), .B(G[10]), .C(G[9]), .D(G[8]), .a_2(a16), .b_2(b16), .c_2(c16), .d_2(d16), .e(e16), .f(f16),
    .g(g16));
  DECODIFICATOR_7_SEG decodificator_7_seg_14 (
    .A(A[11]), .B(A[10]), .C(A[9]), .D(A[8]), .a_2(a11), .b_2(b11), .c_2(c11), .d_2(d11), .e(e11), .f(f11),
    .g(g11));
  DECODIFICATOR_7_SEG decodificator_7_seg_15 (
    .A(B[11]), .B(B[10]), .C(B[9]), .D(B[8]), .a_2(a12), .b_2(b12), .c_2(c12), .d_2(d12), .e(e12), .f(f12),
    .g(g12));
  DECODIFICATOR_7_SEG decodificator_7_seg_16 (
    .A(C[11]), .B(C[10]), .C(C[9]), .D(C[8]), .a_2(a13), .b_2(b13), .c_2(c13), .d_2(d13), .e(e13), .f(f13),
    .g(g13));
  DECODIFICATOR_7_SEG decodificator_7_seg_17 (
    .A(E[11]), .B(E[10]), .C(E[9]), .D(E[8]), .a_2(a14), .b_2(b14), .c_2(c14), .d_2(d14), .e(e14), .f(f14),
    .g(g14));
  DECODIFICATOR_7_SEG decodificator_7_seg_18 (
    .A(H[11]), .B(H[10]), .C(H[9]), .D(H[8]), .a_2(a17), .b_2(b17), .c_2(c17), .d_2(d17), .e(e17), .f(f17),
    .g(g17));
  DECODIFICATOR_7_SEG decodificator_7_seg_19 (
    .A(I[11]), .B(I[10]), .C(I[9]), .D(I[8]), .a_2(a18), .b_2(b18), .c_2(c18), .d_2(d18), .e(e18), .f(f18),
    .g(g18));
  DECODIFICATOR_7_SEG decodificator_7_seg_20 (
    .A(J[11]), .B(J[10]), .C(J[9]), .D(J[8]), .a_2(a19), .b_2(b19), .c_2(c19), .d_2(d19), .e(e19), .f(f19),
    .g(g19));
  DECODIFICATOR_7_SEG decodificator_7_seg_21 (
    .A(K[11]), .B(K[10]), .C(K[9]), .D(K[8]), .a_2(a20), .b_2(b20), .c_2(c20), .d_2(d20), .e(e20), .f(f20),
    .g(g20));
  Multiplexer #(.select(2), .enable("false")) multiplexer_43 (
    .in0(a21), .in1(a22), .in2(a23), .in3(a24), .out(multiplexer_43_out), .sel(SEL));
  Multiplexer #(.select(2), .enable("false")) multiplexer_44 (
    .in0(b21), .in1(b22), .in2(b23), .in3(b24), .out(multiplexer_44_out), .sel(SEL));
  Multiplexer #(.select(2), .enable("false")) multiplexer_45 (
    .in0(c21), .in1(c22), .in2(c23), .in3(c24), .out(multiplexer_45_out), .sel(SEL));
  Multiplexer #(.select(2), .enable("false")) multiplexer_46 (
    .in0(d21), .in1(d22), .in2(d23), .in3(d24), .out(multiplexer_46_out), .sel(SEL));
  Multiplexer #(.select(2), .enable("false")) multiplexer_47 (
    .in0(e21), .in1(e22), .in2(e23), .in3(e24), .out(multiplexer_47_out), .sel(SEL));
  Multiplexer #(.select(2), .enable("false")) multiplexer_48 (
    .in0(f21), .in1(f22), .in2(f23), .in3(f24), .out(multiplexer_48_out), .sel(SEL));
  Multiplexer #(.select(2), .enable("false")) multiplexer_49 (
    .in0(g21), .in1(g22), .in2(g23), .in3(g24), .out(multiplexer_49_out), .sel(SEL));
  Multiplexer #(.select(3)) multiplexer_50 (
    .in0(a25), .in1(a26), .in2(a27), .in3(a28), .in4(a29), .in5(a30), .in6(a43), .out(multiplexer_50_out),
    .sel(num), .en(en));  // open: in7
  DECODIFICATOR_7_SEG decodificator_7_seg_22 (
    .A(L[11]), .B(L[10]), .C(L[9]), .D(L[8]), .a_2(a42), .b_2(b42), .c_2(c42), .d_2(d42), .e(e42), .f(f42),
    .g(g42));
  Multiplexer #(.select(3)) multiplexer_51 (
    .in0(b25), .in1(b26), .in2(b27), .in3(b28), .in4(b29), .in5(b30), .in6(b43), .out(multiplexer_51_out),
    .sel(num), .en(en));  // open: in7
  Multiplexer #(.select(3)) multiplexer_52 (
    .in0(c25), .in1(c26), .in2(c27), .in3(c28), .in4(c29), .in5(c30), .in6(c43), .out(multiplexer_52_out),
    .sel(num), .en(en));  // open: in7
  Multiplexer #(.select(3)) multiplexer_53 (
    .in0(d25), .in1(d26), .in2(d27), .in3(d28), .in4(d29), .in5(d30), .in6(d43), .out(multiplexer_53_out),
    .sel(num), .en(en));  // open: in7
  Multiplexer #(.select(3)) multiplexer_54 (
    .in0(e25), .in1(e26), .in2(e27), .in3(e28), .in4(e29), .in5(e30), .in6(e43), .out(multiplexer_54_out),
    .sel(num), .en(en));  // open: in7
  Multiplexer #(.select(3)) multiplexer_55 (
    .in0(f25), .in1(f26), .in2(f27), .in3(f28), .in4(f29), .in5(f30), .in6(f43), .out(multiplexer_55_out),
    .sel(num), .en(en));  // open: in7
  Multiplexer #(.select(3)) multiplexer_56 (
    .in0(g25), .in1(g26), .in2(g27), .in3(g28), .in4(g29), .in5(g30), .in6(g43), .out(multiplexer_56_out),
    .sel(num), .en(en));  // open: in7
  Multiplexer #(.enable("false")) multiplexer_57 (
    .in0(multiplexer_43_out), .in1(multiplexer_50_out), .out(A3), .sel(en));
  Multiplexer #(.enable("false")) multiplexer_58 (
    .in0(multiplexer_45_out), .in1(multiplexer_52_out), .out(C3), .sel(en));
  Multiplexer #(.enable("false")) multiplexer_59 (
    .in0(multiplexer_44_out), .in1(multiplexer_51_out), .out(B3), .sel(en));
  Multiplexer #(.enable("false")) multiplexer_60 (
    .in0(multiplexer_46_out), .in1(multiplexer_53_out), .out(D3), .sel(en));
  Multiplexer #(.enable("false")) multiplexer_61 (
    .in0(multiplexer_47_out), .in1(multiplexer_54_out), .out(E3), .sel(en));
  Multiplexer #(.enable("false")) multiplexer_62 (
    .in0(multiplexer_48_out), .in1(multiplexer_55_out), .out(F3), .sel(en));
  Multiplexer #(.enable("false")) multiplexer_63 (
    .in0(multiplexer_49_out), .in1(multiplexer_56_out), .out(G3), .sel(en));
  DECODIFICATOR_7_SEG decodificator_7_seg_23 (
    .A(B[7]), .B(B[6]), .C(B[5]), .D(B[4]), .a_2(a22), .b_2(b22), .c_2(c22), .d_2(d22), .e(e22), .f(f22),
    .g(g22));
  DECODIFICATOR_7_SEG decodificator_7_seg_24 (
    .A(C[7]), .B(C[6]), .C(C[5]), .D(C[4]), .a_2(a23), .b_2(b23), .c_2(c23), .d_2(d23), .e(e23), .f(f23),
    .g(g23));
  DECODIFICATOR_7_SEG decodificator_7_seg_25 (
    .A(F[7]), .B(F[6]), .C(F[5]), .D(F[4]), .a_2(a25), .b_2(b25), .c_2(c25), .d_2(d25), .e(e25), .f(f25_t),
    .g(g25));
  DECODIFICATOR_7_SEG decodificator_7_seg_26 (
    .A(G[7]), .B(G[6]), .C(G[5]), .D(G[4]), .a_2(a26), .b_2(b26), .c_2(c26), .d_2(d26), .e(e26), .f(f26),
    .g(g26));
  DECODIFICATOR_7_SEG decodificator_7_seg_27 (
    .A(A[7]), .B(A[6]), .C(A[5]), .D(A[4]), .a_2(a21), .b_2(b21), .c_2(c21), .d_2(d21), .e(e21), .f(f21),
    .g(g21));
  DECODIFICATOR_7_SEG decodificator_7_seg_28 (
    .A(E[7]), .B(E[6]), .C(E[5]), .D(E[4]), .a_2(a24), .b_2(b24), .c_2(c24), .d_2(d24), .e(e24), .f(f24),
    .g(g24));
  DECODIFICATOR_7_SEG decodificator_7_seg_29 (
    .A(H[7]), .B(H[6]), .C(H[5]), .D(H[4]), .a_2(a27), .b_2(b27), .c_2(c27), .d_2(d27), .e(e27), .f(f27),
    .g(g27));
  DECODIFICATOR_7_SEG decodificator_7_seg_30 (
    .A(I[7]), .B(I[6]), .C(I[5]), .D(I[4]), .a_2(a28), .b_2(b28), .c_2(c28), .d_2(d28), .e(e28), .f(f28),
    .g(g28));
  DECODIFICATOR_7_SEG decodificator_7_seg_31 (
    .A(J[7]), .B(J[6]), .C(J[5]), .D(J[4]), .a_2(a29), .b_2(b29), .c_2(c29), .d_2(d29), .e(e29), .f(f29),
    .g(g29));
  DECODIFICATOR_7_SEG decodificator_7_seg_32 (
    .A(K[7]), .B(K[6]), .C(K[5]), .D(K[4]), .a_2(a30), .b_2(b30), .c_2(c30), .d_2(d30), .e(e30), .f(f30),
    .g(g30));
  Multiplexer #(.select(2), .enable("false")) multiplexer_64 (
    .in0(a31), .in1(a32), .in2(a33), .in3(a34), .out(multiplexer_64_out), .sel(SEL));
  Multiplexer #(.select(2), .enable("false")) multiplexer_65 (
    .in0(b31), .in1(b32), .in2(b33), .in3(b34), .out(multiplexer_65_out), .sel(SEL));
  Multiplexer #(.select(2), .enable("false")) multiplexer_66 (
    .in0(c31), .in1(c32), .in2(c33), .in3(c34), .out(multiplexer_66_out), .sel(SEL));
  Multiplexer #(.select(2), .enable("false")) multiplexer_67 (
    .in0(d31), .in1(d32), .in2(d33), .in3(d34), .out(multiplexer_67_out), .sel(SEL));
  Multiplexer #(.select(2), .enable("false")) multiplexer_68 (
    .in0(e31), .in1(e32), .in2(e33), .in3(e34), .out(multiplexer_68_out), .sel(SEL));
  Multiplexer #(.select(2), .enable("false")) multiplexer_69 (
    .in0(f31), .in1(f32), .in2(f33), .in3(f34), .out(multiplexer_69_out), .sel(SEL));
  Multiplexer #(.select(2), .enable("false")) multiplexer_70 (
    .in0(g31), .in1(g32), .in2(g33), .in3(g34), .out(multiplexer_70_out), .sel(SEL));
  Multiplexer #(.select(3)) multiplexer_71 (
    .in0(a35), .in1(a36), .in2(a37), .in3(a38), .in4(a39), .in5(a40), .in6(a44), .out(multiplexer_71_out),
    .sel(num), .en(en));  // open: in7
  Multiplexer #(.select(3)) multiplexer_72 (
    .in0(b35), .in1(b36), .in2(b37), .in3(b38), .in4(b39), .in5(b40), .in6(b44), .out(multiplexer_72_out),
    .sel(num), .en(en));  // open: in7
  Multiplexer #(.select(3)) multiplexer_73 (
    .in0(c35), .in1(c36), .in2(c37), .in3(c38), .in4(c39), .in5(c40), .in6(c44), .out(multiplexer_73_out),
    .sel(num), .en(en));  // open: in7
  Multiplexer #(.select(3)) multiplexer_74 (
    .in0(d35), .in1(d36), .in2(d37), .in3(d38), .in4(d39), .in5(d40), .in6(d44), .out(multiplexer_74_out),
    .sel(num), .en(en));  // open: in7
  Multiplexer #(.select(3)) multiplexer_75 (
    .in0(e35), .in1(e36), .in2(e37), .in3(e38), .in4(e39), .in5(e40), .in6(e44), .out(multiplexer_75_out),
    .sel(num), .en(en));  // open: in7
  Multiplexer #(.select(3)) multiplexer_76 (
    .in0(f35), .in1(f36), .in2(f37), .in3(f38), .in4(f39), .in5(f40), .in6(f44), .out(multiplexer_76_out),
    .sel(num), .en(en));  // open: in7
  Multiplexer #(.select(3)) multiplexer_77 (
    .in0(g35), .in1(g36), .in2(g37), .in3(g38), .in4(g39), .in5(g40), .in6(g44), .out(multiplexer_77_out),
    .sel(num), .en(en));  // open: in7
  DECODIFICATOR_7_SEG decodificator_7_seg_33 (
    .A(L[7]), .B(L[6]), .C(L[5]), .D(L[4]), .a_2(a43), .b_2(b43), .c_2(c43), .d_2(d43), .e(e43), .f(f43),
    .g(g43));
  Multiplexer #(.enable("false")) multiplexer_78 (
    .in0(multiplexer_64_out), .in1(multiplexer_71_out), .out(A4), .sel(en));
  Multiplexer #(.enable("false")) multiplexer_79 (
    .in0(multiplexer_65_out), .in1(multiplexer_72_out), .out(B4), .sel(en));
  Multiplexer #(.enable("false")) multiplexer_80 (
    .in0(multiplexer_66_out), .in1(multiplexer_73_out), .out(C4), .sel(en));
  Multiplexer #(.enable("false")) multiplexer_81 (
    .in0(multiplexer_67_out), .in1(multiplexer_74_out), .out(D4), .sel(en));
  Multiplexer #(.enable("false")) multiplexer_82 (
    .in0(multiplexer_68_out), .in1(multiplexer_75_out), .out(E4), .sel(en));
  Multiplexer #(.enable("false")) multiplexer_83 (
    .in0(multiplexer_69_out), .in1(multiplexer_76_out), .out(F4), .sel(en));
  Multiplexer #(.enable("false")) multiplexer_84 (
    .in0(multiplexer_70_out), .in1(multiplexer_77_out), .out(G4), .sel(en));
  DECODIFICATOR_7_SEG decodificator_7_seg_34 (
    .A(F[3]), .B(F[2]), .C(F[1]), .D(F[0]), .a_2(a35), .b_2(b35), .c_2(c35), .d_2(d35), .e(e35), .f(f35),
    .g(g35));
  DECODIFICATOR_7_SEG decodificator_7_seg_35 (
    .A(G[3]), .B(G[2]), .C(G[1]), .D(G[0]), .a_2(a36), .b_2(b36), .c_2(c36), .d_2(d36), .e(e36), .f(f36),
    .g(g36));
  DECODIFICATOR_7_SEG decodificator_7_seg_36 (
    .A(A[3]), .B(A[2]), .C(A[1]), .D(A[0]), .a_2(a31), .b_2(b31), .c_2(c31), .d_2(d31), .e(e31), .f(f31),
    .g(g31));
  DECODIFICATOR_7_SEG decodificator_7_seg_37 (
    .A(B[3]), .B(B[2]), .C(B[1]), .D(B[0]), .a_2(a32), .b_2(b32), .c_2(c32), .d_2(d32), .e(e32), .f(f32),
    .g(g32));
  DECODIFICATOR_7_SEG decodificator_7_seg_38 (
    .A(C[3]), .B(C[2]), .C(C[1]), .D(C[0]), .a_2(a33), .b_2(b33), .c_2(c33), .d_2(d33), .e(e33), .f(f33),
    .g(g33));
  DECODIFICATOR_7_SEG decodificator_7_seg_39 (
    .A(E[3]), .B(E[2]), .C(E[1]), .D(E[0]), .a_2(a34), .b_2(b34), .c_2(c34), .d_2(d34), .e(e34), .f(f34),
    .g(g34));
  DECODIFICATOR_7_SEG decodificator_7_seg_40 (
    .A(H[3]), .B(H[2]), .C(H[1]), .D(H[0]), .a_2(a37), .b_2(b37), .c_2(c37), .d_2(d37), .e(e37), .f(f37),
    .g(g37));
  DECODIFICATOR_7_SEG decodificator_7_seg_41 (
    .A(I[3]), .B(I[2]), .C(I[1]), .D(I[0]), .a_2(a38), .b_2(b38), .c_2(c38), .d_2(d38), .e(e38), .f(f38),
    .g(g38));
  DECODIFICATOR_7_SEG decodificator_7_seg_42 (
    .A(J[3]), .B(J[2]), .C(J[1]), .D(J[0]), .a_2(a39), .b_2(b39), .c_2(c39), .d_2(d39), .e(e39), .f(f39),
    .g(g39));
  DECODIFICATOR_7_SEG decodificator_7_seg_43 (
    .A(K[3]), .B(K[2]), .C(K[1]), .D(K[0]), .a_2(a40), .b_2(b40), .c_2(c40), .d_2(d40), .e(e40), .f(f40),
    .g(g40));
  DECODIFICATOR_7_SEG decodificator_7_seg_44 (
    .A(L[3]), .B(L[2]), .C(L[1]), .D(L[0]), .a_2(a44), .b_2(b44), .c_2(c44), .d_2(d44), .e(e44), .f(f44),
    .g(g44));
endmodule

module DIVIZOR_FRECVENTA (
  input  CLOCK,
  output CLOCK_2
);

  wire and_1_out, and_2_out, and_3_out, and_4_out, and_5_out, and_6_out, and_7_out, and_8_out, and_9_out,
       and_10_out, and_11_out, and_12_out, not_1_out, not_2_out, not_3_out, not_4_out, not_5_out, not_6_out,
       not_7_out, not_8_out, not_9_out, not_10_out, not_11_out, not_12_out, or_1_out, or_2_out, or_3_out;
  wire [3:0] d_ff_4_q;

  not not_1 (not_1_out, d_ff_4_q[3]);
  and and_1 (and_1_out, not_1_out, not_2_out);
  not not_2 (not_2_out, d_ff_4_q[2]);
  and and_2 (and_2_out, d_ff_4_q[1], d_ff_4_q[0]);
  not not_3 (not_3_out, d_ff_4_q[3]);
  and and_3 (and_3_out, not_3_out, d_ff_4_q[2]);
  not not_4 (not_4_out, d_ff_4_q[1]);
  not not_5 (not_5_out, d_ff_4_q[3]);
  not not_6 (not_6_out, d_ff_4_q[3]);
  and and_4 (and_4_out, not_6_out, not_7_out);
  not not_7 (not_7_out, d_ff_4_q[1]);
  not not_8 (not_8_out, d_ff_4_q[3]);
  and and_5 (and_5_out, not_8_out, d_ff_4_q[1]);
  not not_9 (not_9_out, d_ff_4_q[0]);
  not not_10 (not_10_out, d_ff_4_q[3]);
  and and_6 (and_6_out, not_10_out, not_11_out);
  not not_11 (not_11_out, d_ff_4_q[0]);
  D_Flip_Flop d_ff_1 (.clk(CLOCK), .D(1'b0), .Q(d_ff_4_q[3]), .en(1'b1));  // open: Qn, preset, reset
  and and_7 (and_7_out, and_1_out, and_2_out);
  and and_8 (and_8_out, and_3_out, not_4_out);
  and and_9 (and_9_out, not_5_out, d_ff_4_q[2]);
  not not_12 (not_12_out, d_ff_4_q[0]);
  and and_10 (and_10_out, and_4_out, d_ff_4_q[0]);
  and and_11 (and_11_out, and_5_out, not_9_out);
  D_Flip_Flop d_ff_2 (.clk(CLOCK), .D(or_3_out), .Q(d_ff_4_q[2]), .en(1'b1));  // open: Qn, preset, reset
  or or_1 (or_1_out, and_7_out, and_8_out);
  and and_12 (and_12_out, and_9_out, not_12_out);
  or or_2 (or_2_out, and_10_out, and_11_out);
  D_Flip_Flop d_ff_3 (.clk(CLOCK), .D(or_2_out), .Q(d_ff_4_q[1]), .en(1'b1));  // open: Qn, preset, reset
  or or_3 (or_3_out, or_1_out, and_12_out);
  D_Flip_Flop d_ff_4 (.clk(CLOCK), .D(and_6_out), .Q(d_ff_4_q[0]), .en(1'b1));  // open: Qn, preset, reset
  Decoder #(.select(4), .enable("false")) decoder_1 (
    .out7(CLOCK_2), .sel(d_ff_4_q));  // open: out0, out1, out2, out3, out4, out5, out6, out8, out9, out10, out11, out12, out13, out14, out15
endmodule

module DECODIFICATOR_7_SEG (
  input  A,
  input  B,
  input  C,
  input  D,
  output a_2,
  output b_2,
  output c_2,
  output d_2,
  output e,
  output f,
  output g
);

  wire and_1_out, and_2_out, and_3_out, and_4_out, and_5_out, and_6_out, and_7_out, and_8_out, and_9_out,
       and_10_out, and_11_out, and_12_out, and_13_out, and_14_out, and_15_out, and_16_out, and_17_out,
       not_1_out, not_2_out, not_3_out, not_4_out, not_5_out, not_6_out, not_7_out, not_8_out, not_9_out,
       not_10_out, not_11_out, not_12_out, not_13_out, not_14_out, not_15_out, not_16_out, not_17_out,
       not_18_out, not_19_out, not_20_out, not_21_out, or_1_out, or_2_out, or_3_out, or_4_out, or_6_out,
       or_8_out, or_9_out, or_10_out, or_11_out, or_14_out, or_15_out;

  not not_1 (not_1_out, B);
  and and_1 (and_1_out, not_1_out, not_2_out);
  not not_2 (not_2_out, D);
  and and_2 (and_2_out, B, D);
  not not_3 (not_3_out, B);
  not not_4 (not_4_out, C);
  and and_3 (and_3_out, not_4_out, not_5_out);
  not not_5 (not_5_out, D);
  not not_6 (not_6_out, C);
  or or_1 (or_1_out, not_6_out, D);
  not not_7 (not_7_out, B);
  and and_4 (and_4_out, not_7_out, not_8_out);
  not not_8 (not_8_out, D);
  not not_9 (not_9_out, B);
  and and_5 (and_5_out, not_9_out, C);
  not not_10 (not_10_out, D);
  and and_6 (and_6_out, B, not_11_out);
  not not_11 (not_11_out, C);
  not not_12 (not_12_out, B);
  and and_7 (and_7_out, not_12_out, not_13_out);
  not not_13 (not_13_out, D);
  and and_8 (and_8_out, C, not_14_out);
  not not_14 (not_14_out, D);
  not not_15 (not_15_out, C);
  and and_9 (and_9_out, not_15_out, not_16_out);
  not not_16 (not_16_out, D);
  and and_10 (and_10_out, B, not_17_out);
  not not_17 (not_17_out, C);
  and and_11 (and_11_out, B, not_18_out);
  not not_18 (not_18_out, D);
  not not_19 (not_19_out, B);
  and and_12 (and_12_out, not_19_out, C);
  and and_13 (and_13_out, B, not_20_out);
  not not_20 (not_20_out, C);
  and and_14 (and_14_out, B, not_21_out);
  not not_21 (not_21_out, D);
  or or_2 (or_2_out, and_1_out, C);
  or or_3 (or_3_out, and_2_out, A);
  or or_4 (or_4_out, not_3_out, and_3_out);
  and and_15 (and_15_out, C, D);
  or or_5 (c_2, or_1_out, B);
  or or_6 (or_6_out, and_4_out, and_5_out);
  and and_16 (and_16_out, C, not_10_out);
  and and_17 (and_17_out, and_6_out, D);
  or or_7 (e, and_7_out, and_8_out);
  or or_8 (or_8_out, and_9_out, and_10_out);
  or or_9 (or_9_out, and_11_out, A);
  or or_10 (or_10_out, and_12_out, and_13_out);
  or or_11 (or_11_out, and_14_out, A);
  or or_12 (a_2, or_2_out, or_3_out);
  or or_13 (b_2, or_4_out, and_15_out);
  or or_14 (or_14_out, or_6_out, and_16_out);
  or or_15 (or_15_out, and_17_out, A);
  or or_16 (f, or_8_out, or_9_out);
  or or_17 (g, or_10_out, or_11_out);
  or or_18 (d_2, or_14_out, or_15_out);
endmodule

module NUMARATOR_SUMA (
  input  MODE,
  input  CLOCK,
  input  SW,
  input  ENTER,
  output [3:0] out_5
);

  wire and_1_out, and_2_out, and_3_out, and_4_out, and_5_out, and_6_out, and_7_out, and_8_out, and_9_out,
       and_10_out, and_11_out, and_12_out, and_13_out, not_1_out, not_2_out, not_3_out, not_4_out, not_5_out,
       not_6_out, not_7_out, not_8_out, not_9_out, not_10_out, not_11_out, or_1_out, or_2_out, or_3_out,
       or_4_out, or_5_out;

  and and_1 (and_1_out, out_5[2], out_5[1]);
  not not_1 (not_1_out, out_5[0]);
  not not_2 (not_2_out, out_5[2]);
  not not_3 (not_3_out, MODE);
  not not_4 (not_4_out, MODE);
  not not_5 (not_5_out, out_5[3]);
  not not_6 (not_6_out, out_5[1]);
  not not_7 (not_7_out, out_5[0]);
  and and_2 (and_2_out, and_1_out, out_5[0]);
  and and_3 (and_3_out, out_5[3], not_1_out);
  and and_4 (and_4_out, not_2_out, out_5[1]);
  and and_5 (and_5_out, not_3_out, out_5[2]);
  not not_8 (not_8_out, out_5[1]);
  not not_9 (not_9_out, out_5[0]);
  not not_10 (not_10_out, out_5[2]);
  and and_6 (and_6_out, not_4_out, not_5_out);
  and and_7 (and_7_out, not_6_out, out_5[0]);
  not not_11 (not_11_out, out_5[0]);
  or or_1 (or_1_out, and_2_out, and_3_out);
  and and_8 (and_8_out, and_4_out, out_5[0]);
  or or_2 (or_2_out, and_8_out, and_9_out);
  and and_9 (and_9_out, and_5_out, not_8_out);
  and and_10 (and_10_out, out_5[2], not_9_out);
  or or_3 (or_3_out, and_10_out, and_11_out);
  and and_11 (and_11_out, MODE, not_10_out);
  and and_12 (and_12_out, and_6_out, and_7_out);
  or or_4 (or_4_out, and_12_out, and_13_out);
  and and_13 (and_13_out, out_5[1], not_11_out);
  or or_5 (or_5_out, or_2_out, or_3_out);
  D_Flip_Flop d_ff_1 (.clk(CLOCK), .D(or_1_out), .Q(out_5[3]), .en(SW), .reset(ENTER));  // open: Qn, preset
  D_Flip_Flop d_ff_2 (.clk(CLOCK), .D(or_5_out), .Q(out_5[2]), .en(SW), .reset(ENTER));  // open: Qn, preset
  D_Flip_Flop d_ff_3 (.clk(CLOCK), .D(or_4_out), .Q(out_5[1]), .en(SW), .reset(ENTER));  // open: Qn, preset
  D_Flip_Flop d_ff_4 (.clk(CLOCK), .D(not_7_out), .Q(out_5[0]), .en(SW), .reset(ENTER));  // open: Qn, preset
endmodule

// REGISTRU 4 BITI
module MEMORARE_SUMA (
  input  [3:0] NR,
  input  CLOCK,
  input  SW,
  input  R,
  output [3:0] OUT
);

  D_Flip_Flop d_ff_1 (.clk(CLOCK), .D(NR[3]), .Q(OUT[3]), .en(SW), .reset(R));  // open: Qn, preset
  D_Flip_Flop d_ff_2 (.clk(CLOCK), .D(NR[2]), .Q(OUT[2]), .en(SW), .reset(R));  // open: Qn, preset
  D_Flip_Flop d_ff_3 (.clk(CLOCK), .D(NR[1]), .Q(OUT[1]), .en(SW), .reset(R));  // open: Qn, preset
  D_Flip_Flop d_ff_4 (.clk(CLOCK), .D(NR[0]), .Q(OUT[0]), .en(SW), .reset(R));  // open: Qn, preset
endmodule

module sumator_1_bit (
  input  E,
  input  A,
  input  B,
  input  CIN,
  output S,
  output COUT
);

  wire and_1_out, and_2_out, and_3_out, and_4_out, and_5_out, and_6_out, and_7_out, and_8_out, and_9_out,
       and_10_out, and_11_out, and_12_out, and_13_out, and_14_out, and_15_out, and_16_out, and_17_out,
       and_18_out, not_1_out, not_2_out, not_3_out, not_4_out, not_5_out, not_6_out, or_1_out, or_2_out,
       or_3_out;

  and and_1 (and_1_out, E, not_1_out);
  not not_1 (not_1_out, A);
  not not_2 (not_2_out, B);
  and and_2 (and_2_out, not_2_out, CIN);
  and and_3 (and_3_out, E, not_3_out);
  not not_3 (not_3_out, A);
  and and_4 (and_4_out, B, not_4_out);
  not not_4 (not_4_out, CIN);
  and and_5 (and_5_out, E, A);
  not not_5 (not_5_out, B);
  and and_6 (and_6_out, not_5_out, not_6_out);
  not not_6 (not_6_out, CIN);
  and and_7 (and_7_out, E, A);
  and and_8 (and_8_out, B, CIN);
  and and_9 (and_9_out, E, B);
  and and_10 (and_10_out, E, A);
  and and_11 (and_11_out, and_1_out, and_2_out);
  and and_12 (and_12_out, and_3_out, and_4_out);
  and and_13 (and_13_out, and_5_out, and_6_out);
  and and_14 (and_14_out, and_7_out, and_8_out);
  and and_15 (and_15_out, and_9_out, CIN);
  or or_1 (or_1_out, and_15_out, and_16_out);
  and and_16 (and_16_out, and_10_out, CIN);
  and and_17 (and_17_out, E, A);
  and and_18 (and_18_out, and_17_out, B);
  or or_2 (or_2_out, and_11_out, and_12_out);
  or or_3 (or_3_out, and_13_out, and_14_out);
  or or_4 (COUT, or_1_out, and_18_out);
  or or_5 (S, or_2_out, or_3_out);
endmodule

module SUMATOR_4_BITI (
  input  EN,
  input  [3:0] in_2,
  input  [3:0] in_3,
  input  CIN,
  output [3:0] OUT,
  output CARRY
);

  wire sumator_1_bit_1_cout, sumator_1_bit_2_cout, sumator_1_bit_3_cout;

  sumator_1_bit sumator_1_bit_1 (.E(EN), .A(in_2[0]), .B(in_3[0]), .CIN(CIN), .S(OUT[0]), .COUT(sumator_1_bit_1_cout));
  sumator_1_bit sumator_1_bit_2 (
    .E(EN), .A(in_2[1]), .B(in_3[1]), .CIN(sumator_1_bit_1_cout), .S(OUT[1]), .COUT(sumator_1_bit_2_cout));
  sumator_1_bit sumator_1_bit_3 (
    .E(EN), .A(in_2[2]), .B(in_3[2]), .CIN(sumator_1_bit_2_cout), .S(OUT[2]), .COUT(sumator_1_bit_3_cout));
  sumator_1_bit sumator_1_bit_4 (
    .E(EN), .A(in_2[3]), .B(in_3[3]), .CIN(sumator_1_bit_3_cout), .S(OUT[3]), .COUT(CARRY));
endmodule

// SUMATOR BCD
module SUMATOR_BCD_16_BITI (
  input  en,
  input  [15:0] A,
  input  [15:0] B,
  input  C,
  output [15:0] OUT
);

  wire and_1_out, and_2_out, and_3_out, and_4_out, and_5_out, and_6_out, and_7_out, and_8_out,
       sumator_4_biti_1_carry, sumator_4_biti_2_carry, sumator_4_biti_3_carry, sumator_4_biti_5_carry,
       sumator_4_biti_7_carry, sumator_4_biti_8_carry;
  wire [2:2] or_1_out, or_2_out, or_3_out, or_4_out;
  wire [3:0] sumator_4_biti_1_out, sumator_4_biti_3_out, sumator_4_biti_5_out, sumator_4_biti_7_out;

  SUMATOR_4_BITI sumator_4_biti_1 (
    .EN(en), .in_2(A[3:0]), .in_3(B[3:0]), .CIN(C), .OUT(sumator_4_biti_1_out), .CARRY(sumator_4_biti_1_carry));
  SUMATOR_4_BITI sumator_4_biti_2 (
    .EN(en), .in_2(sumator_4_biti_1_out), .in_3({1'b0, {2{or_1_out[2]}}, 1'b0}), .CIN(1'b0), .OUT(OUT[3:0]),
    .CARRY(sumator_4_biti_2_carry));
  and and_1 (and_1_out, sumator_4_biti_1_out[3], sumator_4_biti_1_out[2]);
  and and_2 (and_2_out, sumator_4_biti_1_out[3], sumator_4_biti_1_out[1]);
  or or_1 (or_1_out[2], and_1_out, sumator_4_biti_1_carry, and_2_out);
  SUMATOR_4_BITI sumator_4_biti_3 (
    .EN(en), .in_2(A[7:4]), .in_3(B[7:4]), .CIN(or_1_out[2]), .OUT(sumator_4_biti_3_out),
    .CARRY(sumator_4_biti_3_carry));
  SUMATOR_4_BITI sumator_4_biti_4 (
    .EN(en), .in_2(sumator_4_biti_3_out), .in_3({1'b0, {2{or_2_out[2]}}, 1'b0}), .CIN(1'b0), .OUT(OUT[7:4]));  // open: CARRY
  and and_3 (and_3_out, sumator_4_biti_3_out[3], sumator_4_biti_3_out[2]);
  and and_4 (and_4_out, sumator_4_biti_3_out[3], sumator_4_biti_3_out[1]);
  or or_2 (or_2_out[2], and_3_out, sumator_4_biti_3_carry, and_4_out);
  SUMATOR_4_BITI sumator_4_biti_5 (
    .EN(en), .in_2(A[11:8]), .in_3(B[11:8]), .CIN(or_2_out[2]), .OUT(sumator_4_biti_5_out),
    .CARRY(sumator_4_biti_5_carry));
  SUMATOR_4_BITI sumator_4_biti_6 (
    .EN(en), .in_2(sumator_4_biti_5_out), .in_3({1'b0, {2{or_3_out[2]}}, 1'b0}), .CIN(1'b0), .OUT(OUT[11:8]));  // open: CARRY
  and and_5 (and_5_out, sumator_4_biti_5_out[3], sumator_4_biti_5_out[2]);
  and and_6 (and_6_out, sumator_4_biti_5_out[1], sumator_4_biti_5_out[3]);
  or or_3 (or_3_out[2], and_5_out, sumator_4_biti_5_carry, and_6_out);
  SUMATOR_4_BITI sumator_4_biti_7 (
    .EN(en), .in_2(A[15:12]), .in_3(B[15:12]), .CIN(or_3_out[2]), .OUT(sumator_4_biti_7_out),
    .CARRY(sumator_4_biti_7_carry));
  SUMATOR_4_BITI sumator_4_biti_8 (
    .EN(en), .in_2(sumator_4_biti_7_out), .in_3({1'b0, {2{or_4_out[2]}}, 1'b0}), .CIN(1'b0),
    .OUT(OUT[15:12]), .CARRY(sumator_4_biti_8_carry));
  and and_7 (and_7_out, sumator_4_biti_7_out[3], sumator_4_biti_7_out[2]);
  and and_8 (and_8_out, sumator_4_biti_7_out[1], sumator_4_biti_7_out[3]);
  or or_4 (or_4_out[2], and_7_out, sumator_4_biti_7_carry, and_8_out);
endmodule

// MEMORIE 1 BIT
module MEMORARE_1_BIT (
  input  BUTON,
  input  CLOCK,
  input  RESET,
  output CARD_INTRODUS
);

  D_Flip_Flop d_ff_1 (.clk(CLOCK), .D(BUTON), .Q(CARD_INTRODUS), .en(BUTON), .reset(RESET));  // open: Qn, preset
endmodule

// MEMORIE PIN
module MEM_ROM (
  input  [1:0] A_ROM,
  input  CS_ROM,
  output [3:0] PIN_ROM
);

  ROM #(.addrWidth(2), .dataWidth(4)) rom_1 (.addr(A_ROM), .data(PIN_ROM), .sel(CS_ROM));

  // Notes on the sheet:
  //   contents of rom_1 (hex, n*v repeats v):
  //   d 5 9 3
endmodule

module NUMARATOR_ENTER (
);

  wire and_1_out, and_2_out, and_3_out, and_4_out, and_5_out, and_6_out, and_7_out, button_1_out,
       clock_1_out, d_ff_1_q, d_ff_2_q, d_ff_3_q, not_1_out, not_2_out, not_3_out, not_4_out, not_5_out,
       not_6_out, not_7_out, not_8_out, or_1_out, or_2_out, or_3_out;

  not not_1 (not_1_out, d_ff_2_q);
  not not_2 (not_2_out, d_ff_1_q);
  not not_3 (not_3_out, d_ff_1_q);
  not not_4 (not_4_out, d_ff_3_q);
  not not_5 (not_5_out, d_ff_2_q);
  not not_6 (not_6_out, d_ff_3_q);
  Clock clock_1 (.out(clock_1_out));
  Button button_1 (.out(button_1_out));
  and and_1 (and_1_out, d_ff_2_q, d_ff_3_q);
  and and_2 (and_2_out, d_ff_1_q, not_1_out);
  not not_7 (not_7_out, d_ff_2_q);
  and and_3 (and_3_out, not_2_out, d_ff_2_q);
  not not_8 (not_8_out, d_ff_3_q);
  and and_4 (and_4_out, not_3_out, not_4_out);
  and and_5 (and_5_out, not_5_out, not_6_out);
  or or_1 (or_1_out, and_1_out, and_2_out);
  and and_6 (and_6_out, not_7_out, d_ff_3_q);
  and and_7 (and_7_out, and_3_out, not_8_out);
  or or_2 (or_2_out, and_4_out, and_5_out);
  or or_3 (or_3_out, and_6_out, and_7_out);
  D_Flip_Flop d_ff_1 (.clk(clock_1_out), .D(or_1_out), .Q(d_ff_1_q), .en(button_1_out));  // open: Qn, preset, reset
  D_Flip_Flop d_ff_2 (.clk(clock_1_out), .D(or_3_out), .Q(d_ff_2_q), .en(button_1_out));  // open: Qn, preset, reset
  D_Flip_Flop d_ff_3 (.clk(clock_1_out), .D(or_2_out), .Q(d_ff_3_q), .en(button_1_out));  // open: Qn, preset, reset
endmodule

module MEMORIE_SOLD (
  input  [1:0] COD,
  input  [15:0] I_RAM,
  input  enter,
  input  clkc,
  input  INTRARE_DEMUX_INTEROGARE,
  output [15:0] Sold
);

  RAM #(.addrWidth(2), .dataWidth(16), .bus("separate")) ram_1 (
    .addr(COD), .din(I_RAM), .data(Sold), .str(enter), .sel(1'b1), .clk(clkc), .ld(INTRARE_DEMUX_INTEROGARE));  // open: clr
endmodule

module complement_fata_de_9 (
  input  EN,
  input  [15:0] NR,
  output [3:0] D,
  output [3:0] C,
  output [3:0] B,
  output [3:0] A
);

  wire [3:0] not_1_out, not_2_out, not_3_out, not_4_out, sumator_4_biti_1_out, sumator_4_biti_2_out,
       sumator_4_biti_3_out, sumator_4_biti_4_out;

  assign not_1_out = ~NR[3:0];  // NOT_Gate not_1, 4 bits wide
  assign not_2_out = ~NR[15:12];  // NOT_Gate not_2, 4 bits wide
  assign not_3_out = ~NR[7:4];  // NOT_Gate not_3, 4 bits wide
  assign not_4_out = ~NR[11:8];  // NOT_Gate not_4, 4 bits wide
  SUMATOR_4_BITI sumator_4_biti_1 (
    .EN(EN), .in_2(not_1_out), .in_3(4'b1001), .CIN(1'b0), .OUT(sumator_4_biti_1_out));  // open: CARRY
  SUMATOR_4_BITI sumator_4_biti_2 (
    .EN(EN), .in_2(not_3_out), .in_3(4'b1001), .CIN(1'b0), .OUT(sumator_4_biti_2_out));  // open: CARRY
  SUMATOR_4_BITI sumator_4_biti_3 (
    .EN(EN), .in_2(not_4_out), .in_3(4'b1001), .CIN(1'b0), .OUT(sumator_4_biti_3_out));  // open: CARRY
  SUMATOR_4_BITI sumator_4_biti_4 (
    .EN(EN), .in_2(not_2_out), .in_3(4'b1001), .CIN(1'b0), .OUT(sumator_4_biti_4_out));  // open: CARRY
  SUMATOR_4_BITI sumator_4_biti_5 (
    .EN(EN), .in_2(sumator_4_biti_1_out), .in_3(4'b0001), .CIN(1'b0), .OUT(D));  // open: CARRY
  SUMATOR_4_BITI sumator_4_biti_6 (
    .EN(EN), .in_2(sumator_4_biti_2_out), .in_3(4'b0001), .CIN(1'b0), .OUT(C));  // open: CARRY
  SUMATOR_4_BITI sumator_4_biti_7 (
    .EN(EN), .in_2(sumator_4_biti_3_out), .in_3(4'b0001), .CIN(1'b0), .OUT(B));  // open: CARRY
  SUMATOR_4_BITI sumator_4_biti_8 (
    .EN(EN), .in_2(sumator_4_biti_4_out), .in_3(4'b0001), .CIN(1'b0), .OUT(A));  // open: CARRY
endmodule

// SCAZATOR BCD
module SCAZATOR (
  input  EN,
  input  [15:0] A,
  input  [15:0] B,
  output [15:0] out_4
);

  wire [15:0] complement_fata_de_9_1_d;

  complement_fata_de_9 complement_fata_de_9_1 (
    .EN(EN), .NR(B), .D(complement_fata_de_9_1_d[3:0]), .C(complement_fata_de_9_1_d[7:4]),
    .B(complement_fata_de_9_1_d[11:8]), .A(complement_fata_de_9_1_d[15:12]));
  SUMATOR_BCD_16_BITI sumator_bcd_16_biti_1 (.A(A), .B(complement_fata_de_9_1_d), .C(EN), .OUT(out_4), .en(EN));
endmodule

module COMPARATOR_1000 (
  input  enable,
  input  [15:0] A,
  input  clock,
  input  [15:0] B,
  output LD,
  output OK
);

  wire comp4_biti_1_egal, comp4_biti_1_mic;

  comp4_biti comp4_biti_1 (
    .A(A[15:12]), .MARE(OK), .EGAL(comp4_biti_1_egal), .MIC(comp4_biti_1_mic), .CLK(clock), .ENTER(enable),
    .B(B[15:12]));
  or or_1 (LD, comp4_biti_1_mic, comp4_biti_1_egal);
endmodule

// COMPARATOR SOLD
module COMP_SOLD (
  input  ENABLE,
  input  clock,
  input  [15:0] A,
  input  [15:0] B,
  output SOLD_OK,
  output LD
);

  wire comp4_biti_1_egal, comp4_biti_1_mare, comp4_biti_1_mic, comp4_biti_2_egal, comp4_biti_2_mare,
       comp4_biti_2_mic, comp4_biti_3_egal, comp4_biti_3_mare, comp4_biti_3_mic, comp4_biti_4_egal,
       comp4_biti_4_mare, comp4_biti_4_mic;

  comp4_biti comp4_biti_1 (
    .A(A[15:12]), .MARE(comp4_biti_1_mare), .EGAL(comp4_biti_1_egal), .MIC(comp4_biti_1_mic), .CLK(clock),
    .ENTER(ENABLE), .B(B[15:12]));
  comp4_biti comp4_biti_2 (
    .A(A[11:8]), .MARE(comp4_biti_2_mare), .EGAL(comp4_biti_2_egal), .MIC(comp4_biti_2_mic), .CLK(clock),
    .ENTER(comp4_biti_1_egal), .B(B[11:8]));
  comp4_biti comp4_biti_3 (
    .A(A[7:4]), .MARE(comp4_biti_3_mare), .EGAL(comp4_biti_3_egal), .MIC(comp4_biti_3_mic), .CLK(clock),
    .ENTER(comp4_biti_2_egal), .B(B[7:4]));
  or or_1 (SOLD_OK, comp4_biti_2_mare, comp4_biti_1_mare, comp4_biti_3_mare, comp4_biti_4_mare, comp4_biti_4_egal);
  comp4_biti comp4_biti_4 (
    .A(A[3:0]), .MARE(comp4_biti_4_mare), .EGAL(comp4_biti_4_egal), .MIC(comp4_biti_4_mic), .CLK(clock),
    .ENTER(comp4_biti_3_egal), .B(B[3:0]));
  or or_2 (LD, comp4_biti_1_mic, comp4_biti_2_mic, comp4_biti_3_mic, comp4_biti_4_mic);
endmodule

module algoritm (
  input  R,
  input  EN,
  input  [15:0] SUMA,
  input  clk,
  output [15:0] out_5,
  output [15:0] _500,
  output [15:0] _200,
  output [15:0] _100,
  output [15:0] _50,
  output [15:0] _20,
  output [15:0] _10,
  output [15:0] _5,
  output [2:0] NUM
);

  wire comparator_1_eq, comparator_1_gt, comparator_1_lt, controlled_buffer_1_out, d_ff_1_q, d_ff_2_q,
       d_ff_2_qn, demultiplexer_1_out0, demultiplexer_1_out1, demultiplexer_1_out2, demultiplexer_1_out3,
       demultiplexer_1_out4, demultiplexer_1_out5, demultiplexer_1_out6, divizor_frecventa_1_clock_2,
       or_1_out;
  wire [1:0] numarator_2_biti_1_out, numarator_2_biti_2_out, numarator_2_biti_3_out, numarator_2_biti_4_out,
       numarator_2_biti_5_out, numarator_2_biti_6_out, numarator_2_biti_7_out;
  wire [15:0] rom_1_data, scazator_1_out_4, shift_register_1_q0;

  assign controlled_buffer_1_out = EN ? clk : 1'bz;  // Controlled_Buffer controlled_buffer_1
  num_3_biti num_3_biti_1 (.EN(comparator_1_lt), .clk(divizor_frecventa_1_clock_2), .r(R), .out_4(NUM));
  DIVIZOR_FRECVENTA divizor_frecventa_1 (.CLOCK(controlled_buffer_1_out), .CLOCK_2(divizor_frecventa_1_clock_2));
  D_Flip_Flop d_ff_1 (
    .clk(divizor_frecventa_1_clock_2), .D(or_1_out), .Q(d_ff_1_q), .en(or_1_out));  // open: Qn, preset, reset
  Multiplexer #(.width(16), .enable("false")) multiplexer_1 (
    .in0(SUMA), .in1(shift_register_1_q0), .out(out_5), .sel(d_ff_1_q));
  ROM #(.addrWidth(3), .dataWidth(16)) rom_1 (.addr(NUM), .data(rom_1_data), .sel(EN));
  Comparator #(.width(16), .mode("unsigned")) comparator_1 (
    .a(out_5), .b(rom_1_data), .gt(comparator_1_gt), .eq(comparator_1_eq), .lt(comparator_1_lt));
  or or_1 (or_1_out, comparator_1_gt, comparator_1_eq);
  D_Flip_Flop d_ff_2 (
    .clk(controlled_buffer_1_out), .D(or_1_out), .Q(d_ff_2_q), .Qn(d_ff_2_qn), .en(or_1_out));  // open: preset, reset
  Demultiplexer #(.select(3), .enable("false")) demultiplexer_1 (
    .out0(demultiplexer_1_out0), .out1(demultiplexer_1_out1), .out2(demultiplexer_1_out2),
    .out3(demultiplexer_1_out3), .out4(demultiplexer_1_out4), .out5(demultiplexer_1_out5),
    .out6(demultiplexer_1_out6), .in(or_1_out), .sel(NUM));  // open: out7
  SCAZATOR scazator_1 (.A(out_5), .B(rom_1_data), .out_4(scazator_1_out_4), .EN(d_ff_2_q));
  NUMARATOR_2_BITI numarator_2_biti_1 (
    .CLK(divizor_frecventa_1_clock_2), .ENTER(demultiplexer_1_out0), .OUT(numarator_2_biti_1_out));
  NUMARATOR_2_BITI numarator_2_biti_2 (
    .CLK(divizor_frecventa_1_clock_2), .ENTER(demultiplexer_1_out1), .OUT(numarator_2_biti_2_out));
  NUMARATOR_2_BITI numarator_2_biti_3 (
    .CLK(divizor_frecventa_1_clock_2), .ENTER(demultiplexer_1_out2), .OUT(numarator_2_biti_3_out));
  NUMARATOR_2_BITI numarator_2_biti_4 (
    .CLK(divizor_frecventa_1_clock_2), .ENTER(demultiplexer_1_out3), .OUT(numarator_2_biti_4_out));
  NUMARATOR_2_BITI numarator_2_biti_5 (
    .CLK(divizor_frecventa_1_clock_2), .ENTER(demultiplexer_1_out4), .OUT(numarator_2_biti_5_out));
  NUMARATOR_2_BITI numarator_2_biti_6 (
    .CLK(divizor_frecventa_1_clock_2), .ENTER(demultiplexer_1_out5), .OUT(numarator_2_biti_6_out));
  NUMARATOR_2_BITI numarator_2_biti_7 (
    .CLK(divizor_frecventa_1_clock_2), .ENTER(demultiplexer_1_out6), .OUT(numarator_2_biti_7_out));
  Shift_Register #(.width(16), .length(1)) shift_register_1 (
    .shift(d_ff_2_qn), .clk(divizor_frecventa_1_clock_2), .load(or_1_out), .d0(scazator_1_out_4),
    .q0(shift_register_1_q0));  // open: in, out, clr
  assign _500[3:0] = {{2{1'b0}}, numarator_2_biti_1_out};  // Bit_Extender bit_extender_1
  assign _200[3:0] = {{2{1'b0}}, numarator_2_biti_2_out};  // Bit_Extender bit_extender_2
  assign _100[3:0] = {{2{1'b0}}, numarator_2_biti_3_out};  // Bit_Extender bit_extender_3
  assign _50[3:0] = {{2{1'b0}}, numarator_2_biti_4_out};  // Bit_Extender bit_extender_4
  assign _20[3:0] = {{2{1'b0}}, numarator_2_biti_5_out};  // Bit_Extender bit_extender_5
  assign _10[3:0] = {{2{1'b0}}, numarator_2_biti_6_out};  // Bit_Extender bit_extender_6
  assign _5[3:0] = {{2{1'b0}}, numarator_2_biti_7_out};  // Bit_Extender bit_extender_7

  assign _5[15:4] = 12'h5;
  assign _10[15:4] = 12'h10;
  assign _20[15:4] = 12'h20;
  assign _50[15:4] = 12'h50;
  assign _100[15:4] = 12'h100;
  assign _200[15:4] = 12'h200;
  assign _500[15:4] = 12'h500;

  // Notes on the sheet:
  //   contents of rom_1 (hex, n*v repeats v):
  //   500 200 100 50 20 10 5
endmodule

module num_3_biti (
  input  EN,
  input  clk,
  input  r,
  output [2:0] out_4
);

  wire and_1_out, and_2_out, and_3_out, and_4_out, and_5_out, and_6_out, and_7_out, not_1_out, not_2_out,
       not_3_out, not_4_out, not_5_out, not_6_out, not_7_out, not_8_out, or_1_out, or_2_out, or_3_out;

  not not_1 (not_1_out, out_4[1]);
  not not_2 (not_2_out, out_4[2]);
  not not_3 (not_3_out, out_4[2]);
  not not_4 (not_4_out, out_4[0]);
  not not_5 (not_5_out, out_4[1]);
  not not_6 (not_6_out, out_4[0]);
  and and_1 (and_1_out, out_4[1], out_4[0]);
  and and_2 (and_2_out, out_4[2], not_1_out);
  not not_7 (not_7_out, out_4[1]);
  and and_3 (and_3_out, not_2_out, out_4[1]);
  not not_8 (not_8_out, out_4[0]);
  and and_4 (and_4_out, not_3_out, not_4_out);
  and and_5 (and_5_out, not_5_out, not_6_out);
  or or_1 (or_1_out, and_1_out, and_2_out);
  and and_6 (and_6_out, not_7_out, out_4[0]);
  and and_7 (and_7_out, and_3_out, not_8_out);
  or or_2 (or_2_out, and_4_out, and_5_out);
  or or_3 (or_3_out, and_6_out, and_7_out);
  D_Flip_Flop d_ff_1 (.clk(clk), .D(or_1_out), .Q(out_4[2]), .en(EN), .reset(r));  // open: Qn, preset
  D_Flip_Flop d_ff_2 (.clk(clk), .D(or_3_out), .Q(out_4[1]), .en(EN), .reset(r));  // open: Qn, preset
  D_Flip_Flop d_ff_3 (.clk(clk), .D(or_2_out), .Q(out_4[0]), .en(EN), .reset(r));  // open: Qn, preset
endmodule
